// Logisim project F3_3-bit_4-to-1_selector.circ as structural Verilog: 1 circuit, main circuit main
module main (
  input  A0,
  input  A1,
  input  A2,
  input  B0,
  input  B1,
  input  B2,
  input  C0,
  input  C1,
  input  C2,
  input  D0,
  input  D1,
  input  D2,
  output R0,
  output R1,
  output R2
);

  wire and_1_out, and_2_out, and_3_out, and_4_out, and_5_out, and_6_out, and_7_out, and_8_out, and_9_out,
       and_10_out, and_11_out, and_12_out, and_13_out, and_14_out, and_15_out, and_16_out, and_17_out,
       and_18_out, decoder_1_out0, decoder_1_out1, decoder_2_out0, decoder_2_out1, decoder_3_out0,
       decoder_3_out1, decoder_4_out0, decoder_4_out1, decoder_5_out0, decoder_5_out1, decoder_6_out0,
       decoder_6_out1, decoder_7_out0, decoder_7_out1, decoder_8_out0, decoder_8_out1, decoder_9_out0,
       decoder_9_out1, or_1_out, or_2_out, or_3_out, or_4_out, or_5_out, or_6_out, S_p1, S_p2;

  // DipSwitch #(.number(2)) S: pin names not known; wires that end beside it: S_p1, S_p2
  Decoder #(.enable("false")) decoder_1 (.out0(decoder_1_out0), .out1(decoder_1_out1), .sel(S_p1));
  Decoder #(.enable("false")) decoder_2 (.out0(decoder_2_out0), .out1(decoder_2_out1), .sel(S_p1));
  Decoder #(.enable("false")) decoder_3 (.out0(decoder_3_out0), .out1(decoder_3_out1), .sel(S_p1));
  Decoder #(.enable("false")) decoder_4 (.out0(decoder_4_out0), .out1(decoder_4_out1), .sel(S_p1));
  Decoder #(.enable("false")) decoder_5 (.out0(decoder_5_out0), .out1(decoder_5_out1), .sel(S_p1));
  Decoder #(.enable("false")) decoder_6 (.out0(decoder_6_out0), .out1(decoder_6_out1), .sel(S_p1));
  and and_1 (and_1_out, A0, decoder_3_out0);
  and and_2 (and_2_out, decoder_3_out1, B0);
  and and_3 (and_3_out, A1, decoder_4_out0);
  and and_4 (and_4_out, decoder_4_out1, B1);
  and and_5 (and_5_out, A2, decoder_1_out0);
  and and_6 (and_6_out, decoder_1_out1, B2);
  and and_7 (and_7_out, C0, decoder_5_out0);
  and and_8 (and_8_out, decoder_5_out1, D0);
  and and_9 (and_9_out, C1, decoder_6_out0);
  and and_10 (and_10_out, decoder_6_out1, D1);
  and and_11 (and_11_out, C2, decoder_2_out0);
  and and_12 (and_12_out, decoder_2_out1, D2);
  or or_1 (or_1_out, and_1_out, and_2_out);
  or or_2 (or_2_out, and_3_out, and_4_out);
  or or_3 (or_3_out, and_5_out, and_6_out);
  or or_4 (or_4_out, and_7_out, and_8_out);
  or or_5 (or_5_out, and_9_out, and_10_out);
  or or_6 (or_6_out, and_11_out, and_12_out);
  Decoder #(.enable("false")) decoder_7 (.out0(decoder_7_out0), .out1(decoder_7_out1), .sel(S_p2));
  Decoder #(.enable("false")) decoder_8 (.out0(decoder_8_out0), .out1(decoder_8_out1), .sel(S_p2));
  Decoder #(.enable("false")) decoder_9 (.out0(decoder_9_out0), .out1(decoder_9_out1), .sel(S_p2));
  and and_13 (and_13_out, or_1_out, decoder_7_out0);
  and and_14 (and_14_out, decoder_7_out1, or_4_out);
  and and_15 (and_15_out, or_2_out, decoder_8_out0);
  and and_16 (and_16_out, decoder_8_out1, or_5_out);
  and and_17 (and_17_out, or_3_out, decoder_9_out0);
  and and_18 (and_18_out, decoder_9_out1, or_6_out);
  or or_7 (R0, and_13_out, and_14_out);
  or or_8 (R1, and_15_out, and_16_out);
  or or_9 (R2, and_17_out, and_18_out);

  // Notes on the sheet:
  //   由3个3位2选1拼接而成
endmodule
