// Logisim project F3_4-bit_register.circ as structural Verilog: 2 circuits, main circuit main
module main (
  input  EN
);

  wire CLK_out, decoder_1_out0, decoder_1_out1, decoder_1_out2, decoder_1_out3, decoder_1_out4,
       decoder_1_out5, decoder_1_out6, decoder_1_out7, decoder_1_out8, decoder_1_out9, decoder_1_out10,
       decoder_1_out11, decoder_1_out12, decoder_1_out13, decoder_1_out14, decoder_1_out15, dipswitch_1_p1,
       dipswitch_1_p2, dipswitch_1_p3, dipswitch_1_p4, or_1_out, or_2_out, or_3_out, or_4_out, or_5_out,
       or_6_out, or_7_out, RE_out;
  wire [3:0] dffwithenandre_4_q;

  Button RE (.out(RE_out));
  Button CLK (.out(CLK_out));
  DFFWithENAndRE dffwithenandre_1 (.D(dipswitch_1_p1), .EN(EN), .CLK(CLK_out), .RE(RE_out), .Q(dffwithenandre_4_q[3]));
  Decoder #(.enable("false"), .select(4)) decoder_1 (
    .out0(decoder_1_out0), .out1(decoder_1_out1), .out2(decoder_1_out2), .out3(decoder_1_out3),
    .out4(decoder_1_out4), .out5(decoder_1_out5), .out6(decoder_1_out6), .out7(decoder_1_out7),
    .out8(decoder_1_out8), .out9(decoder_1_out9), .out10(decoder_1_out10), .out11(decoder_1_out11),
    .out12(decoder_1_out12), .out13(decoder_1_out13), .out14(decoder_1_out14), .out15(decoder_1_out15),
    .sel(dffwithenandre_4_q));
  // DipSwitch #(.number(4)) dipswitch_1: pin names not known; wires that end beside it: dipswitch_1_p1, dipswitch_1_p2, dipswitch_1_p3, dipswitch_1_p4
  DFFWithENAndRE dffwithenandre_2 (.D(dipswitch_1_p2), .EN(EN), .CLK(CLK_out), .RE(RE_out), .Q(dffwithenandre_4_q[2]));
  Hex_Digit_Display hex_digit_display_1 (.value(dffwithenandre_4_q));  // open: dp
  or or_1 (or_1_out, decoder_1_out0, decoder_1_out1, decoder_1_out3, decoder_1_out4, decoder_1_out5, decoder_1_out6, decoder_1_out7, decoder_1_out8, decoder_1_out9, decoder_1_out10, decoder_1_out11, decoder_1_out13);
  DFFWithENAndRE dffwithenandre_3 (.D(dipswitch_1_p3), .EN(EN), .CLK(CLK_out), .RE(RE_out), .Q(dffwithenandre_4_q[1]));
  DFFWithENAndRE dffwithenandre_4 (.D(dipswitch_1_p4), .EN(EN), .CLK(CLK_out), .RE(RE_out), .Q(dffwithenandre_4_q[0]));
  or or_2 (or_2_out, decoder_1_out0, decoder_1_out3, decoder_1_out5, decoder_1_out6, decoder_1_out8, decoder_1_out11, decoder_1_out12, decoder_1_out13, decoder_1_out14, decoder_1_out2);
  or or_3 (or_3_out, decoder_1_out0, decoder_1_out6, decoder_1_out8, decoder_1_out10, decoder_1_out11, decoder_1_out12, decoder_1_out13, decoder_1_out14, decoder_1_out15, decoder_1_out2);
  _7_Segment_Display u_7_segment_display_1 (
    .g(or_4_out), .f(or_5_out), .a(or_6_out), .b(or_7_out), .e(or_3_out), .d(or_2_out), .c(or_1_out));  // open: dp
  or or_4 (or_4_out, decoder_1_out3, decoder_1_out4, decoder_1_out5, decoder_1_out6, decoder_1_out8, decoder_1_out9, decoder_1_out10, decoder_1_out11, decoder_1_out13, decoder_1_out14, decoder_1_out15, decoder_1_out2);
  or or_5 (or_5_out, decoder_1_out0, decoder_1_out4, decoder_1_out5, decoder_1_out6, decoder_1_out8, decoder_1_out9, decoder_1_out10, decoder_1_out11, decoder_1_out12, decoder_1_out14, decoder_1_out15);
  or or_6 (or_6_out, decoder_1_out0, decoder_1_out3, decoder_1_out5, decoder_1_out6, decoder_1_out7, decoder_1_out8, decoder_1_out9, decoder_1_out10, decoder_1_out12, decoder_1_out14, decoder_1_out15, decoder_1_out2);
  or or_7 (or_7_out, decoder_1_out0, decoder_1_out1, decoder_1_out3, decoder_1_out4, decoder_1_out7, decoder_1_out8, decoder_1_out9, decoder_1_out10, decoder_1_out13, decoder_1_out2);
endmodule

module DFFWithENAndRE (
  input  D,
  input  EN,
  input  CLK,
  input  RE,
  output Q
);

  wire multiplexer_1_out;

  Multiplexer multiplexer_1 (.in0(Q), .in1(D), .out(multiplexer_1_out), .sel(EN));
  D_Flip_Flop d_ff_1 (.D(multiplexer_1_out), .clk(CLK), .Q(Q), .reset(RE));  // open: Qn, preset
endmodule
