// Logisim project F3_4_Switchable_counter_base_seven-segment_display.circ as structural Verilog: 2 circuits, main circuit main
module main (
);

  wire decoder_1_out0, decoder_1_out1, decoder_1_out2, decoder_1_out3, decoder_1_out4, decoder_1_out5,
       decoder_1_out6, decoder_1_out7, decoder_1_out8, decoder_1_out9, decoder_1_out10, decoder_1_out11,
       decoder_1_out12, decoder_1_out13, decoder_1_out14, decoder_1_out15, decoder_2_out0, decoder_2_out1,
       decoder_2_out2, decoder_2_out3, decoder_2_out4, decoder_2_out5, decoder_2_out6, decoder_2_out7,
       decoder_2_out8, decoder_2_out9, decoder_2_out10, decoder_2_out11, decoder_2_out12, decoder_2_out13,
       decoder_2_out14, decoder_2_out15, dipswitch_1_p5, multiplexer_1_out, multiplexer_2_out,
       multiplexer_3_out, multiplexer_4_out, multiplexer_5_out, multiplexer_6_out, multiplexer_7_out,
       multiplexer_8_out, not_1_out, or_1_out, or_2_out, or_3_out, or_4_out, or_5_out, or_6_out, or_7_out,
       or_8_out, or_9_out, or_10_out, or_11_out, or_12_out, or_13_out, or_14_out, or_15_out;
  wire [3:0] dipswitch_1_p4;

  Decoder #(.enable("false"), .select(4)) decoder_1 (
    .out0(decoder_1_out0), .out1(decoder_1_out1), .out2(decoder_1_out2), .out3(decoder_1_out3),
    .out4(decoder_1_out4), .out5(decoder_1_out5), .out6(decoder_1_out6), .out7(decoder_1_out7),
    .out8(decoder_1_out8), .out9(decoder_1_out9), .out10(decoder_1_out10), .out11(decoder_1_out11),
    .out12(decoder_1_out12), .out13(decoder_1_out13), .out14(decoder_1_out14), .out15(decoder_1_out15),
    .sel(dipswitch_1_p4));
  or or_1 (or_1_out, decoder_1_out0, decoder_1_out1, decoder_1_out3, decoder_1_out4, decoder_1_out5, decoder_1_out6, decoder_1_out7, decoder_1_out8, decoder_1_out9, decoder_1_out10, decoder_1_out11, decoder_1_out13);
  or or_2 (or_2_out, decoder_1_out0, decoder_1_out3, decoder_1_out5, decoder_1_out6, decoder_1_out8, decoder_1_out11, decoder_1_out12, decoder_1_out13, decoder_1_out14, decoder_1_out2);
  or or_3 (or_3_out, decoder_1_out0, decoder_1_out6, decoder_1_out8, decoder_1_out10, decoder_1_out11, decoder_1_out12, decoder_1_out13, decoder_1_out14, decoder_1_out15, decoder_1_out2);
  or or_4 (or_4_out, decoder_1_out3, decoder_1_out4, decoder_1_out5, decoder_1_out6, decoder_1_out8, decoder_1_out9, decoder_1_out10, decoder_1_out11, decoder_1_out13, decoder_1_out14, decoder_1_out15, decoder_1_out2);
  Multiplexer multiplexer_1 (.in0(or_1_out), .in1(or_8_out), .out(multiplexer_1_out), .sel(not_1_out));
  Multiplexer multiplexer_2 (.in0(or_2_out), .in1(or_9_out), .out(multiplexer_2_out), .sel(not_1_out));
  or or_5 (or_5_out, decoder_1_out0, decoder_1_out4, decoder_1_out5, decoder_1_out6, decoder_1_out8, decoder_1_out9, decoder_1_out10, decoder_1_out11, decoder_1_out12, decoder_1_out14, decoder_1_out15);
  Multiplexer multiplexer_3 (.in0(or_3_out), .in1(or_10_out), .out(multiplexer_3_out), .sel(not_1_out));
  // DipSwitch #(.number(5)) dipswitch_1: pin names not known; wires that end beside it: dipswitch_1_p4[3], dipswitch_1_p4[2], dipswitch_1_p4[1], dipswitch_1_p4[0], dipswitch_1_p5
  Multiplexer multiplexer_4 (.in0(or_4_out), .in1(or_11_out), .out(multiplexer_4_out), .sel(not_1_out));
  _7_Segment_Display u_7_segment_display_1 (
    .g(multiplexer_4_out), .f(multiplexer_5_out), .a(multiplexer_6_out), .b(multiplexer_7_out),
    .e(multiplexer_3_out), .d(multiplexer_2_out), .c(multiplexer_1_out), .dp(multiplexer_8_out));
  or or_6 (or_6_out, decoder_1_out0, decoder_1_out3, decoder_1_out5, decoder_1_out6, decoder_1_out7, decoder_1_out8, decoder_1_out9, decoder_1_out10, decoder_1_out12, decoder_1_out14, decoder_1_out15, decoder_1_out2);
  Multiplexer multiplexer_5 (.in0(or_5_out), .in1(or_12_out), .out(multiplexer_5_out), .sel(not_1_out));
  Multiplexer multiplexer_6 (.in0(or_6_out), .in1(or_13_out), .out(multiplexer_6_out), .sel(not_1_out));
  Multiplexer multiplexer_7 (.in0(or_7_out), .in1(or_14_out), .out(multiplexer_7_out), .sel(not_1_out));
  not not_1 (not_1_out, dipswitch_1_p5);
  Multiplexer multiplexer_8 (.in0(1'b0), .in1(or_15_out), .out(multiplexer_8_out), .sel(not_1_out));
  or or_7 (or_7_out, decoder_1_out0, decoder_1_out1, decoder_1_out3, decoder_1_out4, decoder_1_out7, decoder_1_out8, decoder_1_out9, decoder_1_out10, decoder_1_out13, decoder_1_out2);
  Decoder #(.enable("false"), .select(4)) decoder_2 (
    .out0(decoder_2_out0), .out1(decoder_2_out1), .out2(decoder_2_out2), .out3(decoder_2_out3),
    .out4(decoder_2_out4), .out5(decoder_2_out5), .out6(decoder_2_out6), .out7(decoder_2_out7),
    .out8(decoder_2_out8), .out9(decoder_2_out9), .out10(decoder_2_out10), .out11(decoder_2_out11),
    .out12(decoder_2_out12), .out13(decoder_2_out13), .out14(decoder_2_out14), .out15(decoder_2_out15),
    .sel(dipswitch_1_p4));
  or or_8 (or_8_out, decoder_2_out0, decoder_2_out1, decoder_2_out3, decoder_2_out4, decoder_2_out5, decoder_2_out6, decoder_2_out7, decoder_2_out8, decoder_2_out9);
  or or_9 (or_9_out, decoder_2_out0, decoder_2_out3, decoder_2_out5, decoder_2_out6, decoder_2_out8, decoder_2_out2);
  or or_10 (or_10_out, decoder_2_out0, decoder_2_out6, decoder_2_out8, decoder_2_out2);
  or or_11 (or_11_out, decoder_2_out3, decoder_2_out4, decoder_2_out5, decoder_2_out6, decoder_2_out8, decoder_2_out9, decoder_2_out2);
  or or_12 (or_12_out, decoder_2_out0, decoder_2_out4, decoder_2_out5, decoder_2_out6, decoder_2_out8, decoder_2_out9);
  or or_13 (or_13_out, decoder_2_out0, decoder_2_out3, decoder_2_out5, decoder_2_out6, decoder_2_out7, decoder_2_out8, decoder_2_out9, decoder_2_out2);
  or or_14 (or_14_out, decoder_2_out0, decoder_2_out1, decoder_2_out3, decoder_2_out4, decoder_2_out7, decoder_2_out8, decoder_2_out9, decoder_2_out2);
  or or_15 (or_15_out, decoder_2_out10, decoder_2_out11, decoder_2_out13, decoder_2_out14, decoder_2_out15);
endmodule

module DFFWithENAndRE (
  input  D,
  input  EN,
  input  CLK,
  input  RE,
  output Q
);

  wire multiplexer_1_out;

  Multiplexer multiplexer_1 (.in0(Q), .in1(D), .out(multiplexer_1_out), .sel(EN));
  D_Flip_Flop d_ff_1 (.D(multiplexer_1_out), .clk(CLK), .Q(Q), .reset(RE));  // open: Qn, preset
endmodule
