// Logisim project F3_4_bit_adder.circ as structural Verilog: 2 circuits, main circuit main
module main (
);

  wire A_p1, A_p2, A_p3, A_p4, B_p1, B_p2, B_p3, B_p4, full_add_1_co, full_add_2_co, full_add_3_co,
       full_add_4_co;
  wire [3:0] full_add_1_s;

  // DipSwitch #(.number(4)) A: pin names not known; wires that end beside it: A_p1, A_p2, A_p3, A_p4
  // DipSwitch #(.number(4)) B: pin names not known; wires that end beside it: B_p1, B_p2, B_p3, B_p4
  Hex_Digit_Display hex_digit_display_1 (.value(full_add_1_s));  // open: dp
  full_add full_add_1 (.CI(1'b0), .A(A_p4), .B(B_p4), .CO(full_add_1_co), .S(full_add_1_s[0]));
  LED led_1 (.in(full_add_4_co));
  full_add full_add_2 (.CI(full_add_1_co), .A(A_p3), .B(B_p3), .CO(full_add_2_co), .S(full_add_1_s[1]));
  full_add full_add_3 (.CI(full_add_2_co), .A(A_p2), .B(B_p2), .CO(full_add_3_co), .S(full_add_1_s[2]));
  full_add full_add_4 (.CI(full_add_3_co), .A(A_p1), .B(B_p1), .CO(full_add_4_co), .S(full_add_1_s[3]));

  // Notes on the sheet:
  //   +
  //   =
  //   为了方便直接使用16进制数码显示，7段数码管实现方式参照 搭建七段数码管译码器(2)
  //   进位
endmodule

module full_add (
  input  CI,
  input  A,
  input  B,
  output CO,
  output S
);

  wire and_1_out, and_2_out, xor_1_out;

  xor xor_1 (xor_1_out, A, B);
  and and_1 (and_1_out, A, B);
  xor xor_2 (S, CI, xor_1_out);
  and and_2 (and_2_out, CI, xor_1_out);
  or or_1 (CO, and_2_out, and_1_out);
endmodule
