// Logisim project F3_4_bit_counter.circ as structural Verilog: 1 circuit, main circuit main
module main (
);

  wire button_1_out;
  wire [3:0] adder_1_out, d_ff_1_q;

  Adder #(.width(4)) adder_1 (.a(d_ff_1_q), .b(4'b0001), .out(adder_1_out));  // open: cin, cout
  Button button_1 (.out(button_1_out));
  D_Flip_Flop d_ff_1 (.D(adder_1_out[0]), .clk(button_1_out), .Q(d_ff_1_q[0]));  // open: Qn, preset, reset
  D_Flip_Flop d_ff_2 (.D(adder_1_out[1]), .clk(button_1_out), .Q(d_ff_1_q[1]));  // open: Qn, preset, reset
  D_Flip_Flop d_ff_3 (.D(adder_1_out[2]), .clk(button_1_out), .Q(d_ff_1_q[2]));  // open: Qn, preset, reset
  D_Flip_Flop d_ff_4 (.D(adder_1_out[3]), .clk(button_1_out), .Q(d_ff_1_q[3]));  // open: Qn, preset, reset
endmodule
