// Logisim project F3_4_bit_full_min.circ as structural Verilog: 2 circuits, main circuit full_min
module main (
  input  X,
  input  Y,
  output hDi,
  output hBo
);

  wire dipswitch_1_sw1, dipswitch_1_sw2, dipswitch_1_sw3, dipswitch_1_sw4, dipswitch_2_sw1, dipswitch_2_sw2,
       dipswitch_2_sw3, dipswitch_2_sw4, full_min_1_bo, full_min_2_bo, full_min_3_bo, full_min_4_bo,
       not_1_out;
  wire [3:0] full_min_1_di;

  full_min full_min_1 (
    .Xi(dipswitch_1_sw4), .Yi(dipswitch_2_sw4), .Bo(full_min_1_bo), .Di(full_min_1_di[0]));  // open: Bi
  DipSwitch #(.number(4)) dipswitch_1 (
    .sw1(dipswitch_1_sw1), .sw2(dipswitch_1_sw2), .sw3(dipswitch_1_sw3), .sw4(dipswitch_1_sw4));
  xor xor_1 (hDi, X, Y);
  and and_1 (hBo, Y, not_1_out);
  not not_1 (not_1_out, X);
  DipSwitch #(.number(4)) dipswitch_2 (
    .sw1(dipswitch_2_sw1), .sw2(dipswitch_2_sw2), .sw3(dipswitch_2_sw3), .sw4(dipswitch_2_sw4));
  full_min full_min_2 (
    .Bi(full_min_1_bo), .Xi(dipswitch_1_sw3), .Yi(dipswitch_2_sw3), .Bo(full_min_2_bo), .Di(full_min_1_di[1]));
  Hex_Digit_Display hex_digit_display_1 (.value(full_min_1_di));  // open: dp
  LED led_1 (.in(full_min_4_bo));
  full_min full_min_3 (
    .Bi(full_min_2_bo), .Xi(dipswitch_1_sw2), .Yi(dipswitch_2_sw2), .Bo(full_min_3_bo), .Di(full_min_1_di[2]));
  full_min full_min_4 (
    .Bi(full_min_3_bo), .Xi(dipswitch_1_sw1), .Yi(dipswitch_2_sw1), .Bo(full_min_4_bo), .Di(full_min_1_di[3]));

  // Notes on the sheet:
  //   -
  //   =
  //   借位
endmodule

module full_min (
  input  Bi,
  input  Xi,
  input  Yi,
  output Bo,
  output Di
);

  wire and_1_out, and_2_out, not_1_out, not_2_out, xor_1_out;

  not not_1 (not_1_out, Xi);
  xor xor_1 (xor_1_out, Xi, Yi);
  and and_1 (and_1_out, Yi, not_1_out);
  not not_2 (not_2_out, xor_1_out);
  xor xor_2 (Di, xor_1_out, Bi);
  and and_2 (and_2_out, Bi, not_2_out);
  or or_1 (Bo, and_1_out, and_2_out);
endmodule
