// Logisim project F3_4_bit_ones_complement_adder.circ as structural Verilog: 3 circuits, main circuit main
module main (
  output [3:0] out_1
);

  wire [3:0] dipswitch_1_sw4, dipswitch_2_sw4, fbsma_1_r, sam2oc_1_out_2, sam2oc_2_out_2;
  wire [3:3] fbsma_1_r_2;

  DipSwitch #(.number(4)) dipswitch_1 (
    .sw1(dipswitch_1_sw4[3]), .sw2(dipswitch_1_sw4[2]), .sw3(dipswitch_1_sw4[1]), .sw4(dipswitch_1_sw4[0]));
  DipSwitch #(.number(4)) dipswitch_2 (
    .sw1(dipswitch_2_sw4[3]), .sw2(dipswitch_2_sw4[2]), .sw3(dipswitch_2_sw4[1]), .sw4(dipswitch_2_sw4[0]));
  SAM2OC sam2oc_1 (.in_1(dipswitch_1_sw4), .out_2(sam2oc_1_out_2));
  SAM2OC sam2oc_2 (.in_1(dipswitch_2_sw4), .out_2(sam2oc_2_out_2));
  FBSMA fbsma_1 (.A(sam2oc_1_out_2), .B(sam2oc_2_out_2), .NE(fbsma_1_r[3]), .R({fbsma_1_r_2[3], fbsma_1_r[2:0]}));
  _7_Segment_Display u_7_segment_display_1 (.g(fbsma_1_r[3]));  // open: f, a, b, e, d, c, dp
  Hex_Digit_Display hex_digit_display_1 (.value({fbsma_1_r_2[3], fbsma_1_r[2:0]}));  // open: dp
  SAM2OC sam2oc_3 (.in_1(fbsma_1_r), .out_2(out_1));
endmodule

module FBSMA (
  input  [3:0] A,
  input  [3:0] B,
  output NE,
  output [3:0] R
);

  wire adder_1_cout, and_1_out, and_2_out, and_3_out, multiplexer_1_out, not_1_out, not_2_out, not_3_out,
       subtractor_1_bout, subtractor_2_bout, xor_1_out;
  wire [2:0] adder_1_out, multiplexer_3_out, subtractor_1_out, subtractor_2_out;

  Adder #(.width(3)) adder_1 (.a(B[2:0]), .b(A[2:0]), .out(adder_1_out), .cout(adder_1_cout));  // open: cin
  Subtractor #(.width(3)) subtractor_1 (
    .a(A[2:0]), .b(B[2:0]), .out(subtractor_1_out), .bout(subtractor_1_bout));  // open: bin
  Subtractor #(.width(3)) subtractor_2 (
    .a(B[2:0]), .b(A[2:0]), .out(subtractor_2_out), .bout(subtractor_2_bout));  // open: bin
  not not_1 (not_1_out, A[3]);
  Multiplexer multiplexer_1 (
    .in0(subtractor_1_bout), .in1(subtractor_2_bout), .out(multiplexer_1_out), .sel(not_2_out));
  not not_2 (not_2_out, and_1_out);
  and and_1 (and_1_out, B[3], not_1_out);
  xor xor_1 (xor_1_out, B[3], A[3]);
  and and_2 (and_2_out, B[3], A[3]);
  Multiplexer #(.width(3)) multiplexer_2 (.in0(adder_1_out), .in1(multiplexer_3_out), .out(R[2:0]), .sel(xor_1_out));
  Multiplexer #(.width(3)) multiplexer_3 (
    .in0(subtractor_1_out), .in1(subtractor_2_out), .out(multiplexer_3_out), .sel(not_2_out));
  and and_3 (and_3_out, multiplexer_1_out, xor_1_out);
  or or_1 (NE, and_3_out, and_2_out);
  and and_4 (R[3], adder_1_cout, not_3_out);
  not not_3 (not_3_out, xor_1_out);
endmodule

module SAM2OC (
  input  [3:0] in_1,
  output [3:0] out_2
);

  xor xor_1 (out_2[0], in_1[0], in_1[3]);
  xor xor_2 (out_2[1], in_1[1], in_1[3]);
  xor xor_3 (out_2[2], in_1[2], in_1[3]);

  assign out_2[3] = in_1[3];
endmodule
