// Logisim project F3_4_bit_sign_magnitude_adder.circ as structural Verilog: 1 circuit, main circuit main
module main (
);

  wire adder_1_cout, and_1_out, and_2_out, and_3_out, and_4_out, dipswitch_1_sw1, dipswitch_2_sw1,
       multiplexer_1_out, not_1_out, not_2_out, not_3_out, or_1_out, subtractor_1_bout, subtractor_2_bout,
       xor_1_out;
  wire [3:0] adder_1_out, dipswitch_1_sw5, dipswitch_2_sw5, multiplexer_2_out, multiplexer_3_out,
       subtractor_1_out, subtractor_2_out;

  DipSwitch #(.number(5)) dipswitch_1 (
    .sw1(dipswitch_1_sw1), .sw2(dipswitch_1_sw5[3]), .sw3(dipswitch_1_sw5[2]), .sw4(dipswitch_1_sw5[1]),
    .sw5(dipswitch_1_sw5[0]));
  DipSwitch #(.number(5)) dipswitch_2 (
    .sw1(dipswitch_2_sw1), .sw2(dipswitch_2_sw5[3]), .sw3(dipswitch_2_sw5[2]), .sw4(dipswitch_2_sw5[1]),
    .sw5(dipswitch_2_sw5[0]));
  Adder #(.width(4)) adder_1 (
    .a(dipswitch_2_sw5), .b(dipswitch_1_sw5), .out(adder_1_out), .cout(adder_1_cout));  // open: cin
  Subtractor #(.width(4)) subtractor_1 (
    .a(dipswitch_1_sw5), .b(dipswitch_2_sw5), .out(subtractor_1_out), .bout(subtractor_1_bout));  // open: bin
  Subtractor #(.width(4)) subtractor_2 (
    .a(dipswitch_2_sw5), .b(dipswitch_1_sw5), .out(subtractor_2_out), .bout(subtractor_2_bout));  // open: bin
  not not_1 (not_1_out, dipswitch_1_sw1);
  Multiplexer multiplexer_1 (
    .in0(subtractor_1_bout), .in1(subtractor_2_bout), .out(multiplexer_1_out), .sel(not_2_out));
  not not_2 (not_2_out, and_1_out);
  and and_1 (and_1_out, dipswitch_2_sw1, not_1_out);
  xor xor_1 (xor_1_out, dipswitch_2_sw1, dipswitch_1_sw1);
  and and_2 (and_2_out, dipswitch_2_sw1, dipswitch_1_sw1);
  Multiplexer #(.width(4)) multiplexer_2 (
    .in0(adder_1_out), .in1(multiplexer_3_out), .out(multiplexer_2_out), .sel(xor_1_out));
  Multiplexer #(.width(4)) multiplexer_3 (
    .in0(subtractor_1_out), .in1(subtractor_2_out), .out(multiplexer_3_out), .sel(not_2_out));
  and and_3 (and_3_out, multiplexer_1_out, xor_1_out);
  or or_1 (or_1_out, and_3_out, and_2_out);
  _7_Segment_Display u_7_segment_display_1 (.g(or_1_out));  // open: f, a, b, e, d, c, dp
  Hex_Digit_Display hex_digit_display_1 (.value(multiplexer_2_out));  // open: dp
  LED led_1 (.in(and_4_out));
  and and_4 (and_4_out, adder_1_cout, not_3_out);
  not not_3 (not_3_out, xor_1_out);

  // Notes on the sheet:
  //   进位
endmodule
