// Logisim project F3_DFF_with_enable.circ as structural Verilog: 1 circuit, main circuit main
module main (
  input  D,
  input  EN,
  output RES
);

  wire CLK_out, multiplexer_1_out;

  Button CLK (.out(CLK_out));
  D_Flip_Flop d_ff_1 (.D(multiplexer_1_out), .clk(CLK_out), .Q(RES));  // open: Qn, preset, reset
  Multiplexer multiplexer_1 (.in0(RES), .in1(D), .out(multiplexer_1_out), .sel(EN));
endmodule
