// Logisim project F3_DFF_with_reset_function.circ as structural Verilog: 1 circuit, main circuit main
module main (
  input  in_1,
  output Q,
  output out_3,
  output out_4
);

  wire and_1_out, and_2_out, and_3_out, and_4_out, and_5_out, button_1_out, button_2_out, nor_1_out,
       not_1_out, not_2_out, not_3_out, not_4_out, or_1_out;

  Button button_1 (.out(button_1_out));
  not not_1 (not_1_out, button_1_out);
  Button button_2 (.out(button_2_out));
  not not_2 (not_2_out, in_1);
  and and_1 (and_1_out, not_2_out, not_1_out);
  and and_2 (and_2_out, not_1_out, in_1);
  or or_1 (or_1_out, button_1_out, button_2_out);
  nor nor_1 (nor_1_out, and_1_out, out_3);
  nor nor_2 (out_3, nor_1_out, and_2_out);
  and and_3 (and_3_out, nor_1_out, not_3_out);
  not not_3 (not_3_out, button_2_out);
  not not_4 (not_4_out, and_3_out);
  and and_4 (and_4_out, not_4_out, or_1_out);
  and and_5 (and_5_out, or_1_out, and_3_out);
  nor nor_3 (Q, and_4_out, out_4);
  nor nor_4 (out_4, Q, and_5_out);

  // Notes on the sheet:
  //   CLK
  //   D
  //   D
  //   WE
  //   D
  //   RE
  //   R
  //   S
  //   WE
  //   Q
  //   Q_
  //   D
  //   R
  //   S
  //   Q_
endmodule
