// Logisim project F3_DL_with_reset_function.circ as structural Verilog: 1 circuit, main circuit main
module main (
  input  in_1,
  input  D,
  input  in_3,
  output Q,
  output out_5
);

  wire and_1_out, and_2_out, nand_1_out, not_1_out, not_2_out, not_3_out, or_1_out;

  or or_1 (or_1_out, in_1, D);
  not not_1 (not_1_out, D);
  nand nand_1 (nand_1_out, not_1_out, in_3);
  not not_2 (not_2_out, nand_1_out);
  not not_3 (not_3_out, not_2_out);
  and and_1 (and_1_out, not_3_out, or_1_out);
  and and_2 (and_2_out, or_1_out, not_2_out);
  nor nor_1 (Q, and_1_out, out_5);
  nor nor_2 (out_5, Q, and_2_out);

  // Notes on the sheet:
  //   WE
  //   RE
  //   D
  //   WE
  //   R
  //   S
  //   Q_
endmodule
