// Logisim project F3_Detect_overflow_in_twos_complement_addition.circ as structural Verilog: 1 circuit, main circuit main
module main (
  output [3:0] out_1
);

  wire adder_1_cout, adder_2_cout, adder_3_cout, and_1_out, and_2_out, dipswitch_1_sw1, dipswitch_1_sw2,
       dipswitch_1_sw3, dipswitch_1_sw4, dipswitch_2_sw1, dipswitch_2_sw2, dipswitch_2_sw3, dipswitch_2_sw4,
       xnor_1_out, xor_1_out;

  DipSwitch #(.number(4)) dipswitch_1 (
    .sw1(dipswitch_1_sw1), .sw2(dipswitch_1_sw2), .sw3(dipswitch_1_sw3), .sw4(dipswitch_1_sw4));
  DipSwitch #(.number(4)) dipswitch_2 (
    .sw1(dipswitch_2_sw1), .sw2(dipswitch_2_sw2), .sw3(dipswitch_2_sw3), .sw4(dipswitch_2_sw4));
  Adder #(.width(1)) adder_1 (
    .a(dipswitch_2_sw4), .b(dipswitch_1_sw4), .out(out_1[0]), .cout(adder_1_cout));  // open: cin
  Adder #(.width(1)) adder_2 (
    .a(dipswitch_2_sw3), .b(dipswitch_1_sw3), .out(out_1[1]), .cin(adder_1_cout), .cout(adder_2_cout));
  Adder #(.width(1)) adder_3 (
    .a(dipswitch_2_sw2), .b(dipswitch_1_sw2), .out(out_1[2]), .cin(adder_2_cout), .cout(adder_3_cout));
  Adder #(.width(1)) adder_4 (
    .a(dipswitch_2_sw1), .b(dipswitch_1_sw1), .out(out_1[3]), .cin(adder_3_cout));  // open: cout
  and and_1 (and_1_out, dipswitch_1_sw1, dipswitch_2_sw1);
  xnor xnor_1 (xnor_1_out, dipswitch_1_sw1, dipswitch_2_sw1);
  xor xor_1 (xor_1_out, out_1[3], and_1_out);
  and and_2 (and_2_out, xor_1_out, xnor_1_out);
  LED led_1 (.in(and_2_out));
endmodule
