// Logisim project F3_Digital_clock.circ as structural Verilog: 2 circuits, main circuit main
module main (
  input  in_1
);

  wire button_1_out, clock_1_out, comparator_1_eq, comparator_2_eq, dec_counter_1_c, dec_counter_2_c,
       or_1_out, or_2_out;
  wire [3:0] dec_counter_1_q, dec_counter_2_q, dec_counter_3_q, dec_counter_4_q;

  Clock clock_1 (.out(clock_1_out));
  Button button_1 (.out(button_1_out));
  or or_1 (or_1_out, button_1_out, comparator_2_eq);
  or or_2 (or_2_out, button_1_out, comparator_1_eq);
  Hex_Digit_Display hex_digit_display_1 (.value(dec_counter_4_q));  // open: dp
  Hex_Digit_Display hex_digit_display_2 (.value(dec_counter_2_q));  // open: dp
  Hex_Digit_Display hex_digit_display_3 (.value(dec_counter_3_q));  // open: dp
  DEC_Counter dec_counter_1 (.WE(in_1), .CLK(clock_1_out), .R(or_2_out), .Q(dec_counter_1_q), .C(dec_counter_1_c));
  Hex_Digit_Display hex_digit_display_4 (.value(dec_counter_1_q));  // open: dp
  DEC_Counter dec_counter_2 (.WE(in_1), .CLK(comparator_1_eq), .R(or_1_out), .Q(dec_counter_2_q), .C(dec_counter_2_c));
  DEC_Counter dec_counter_3 (.WE(in_1), .CLK(dec_counter_1_c), .R(or_2_out), .Q(dec_counter_3_q));  // open: C
  DEC_Counter dec_counter_4 (.WE(in_1), .CLK(dec_counter_2_c), .R(or_1_out), .Q(dec_counter_4_q));  // open: C
  Comparator #(.width(4)) comparator_1 (.a(dec_counter_3_q), .b(4'b0110), .eq(comparator_1_eq));  // open: gt, lt
  Comparator #(.width(4)) comparator_2 (.a(dec_counter_4_q), .b(4'b0110), .eq(comparator_2_eq));  // open: gt, lt
endmodule

module DEC_Counter (
  input  WE,
  input  CLK,
  input  R,
  output [3:0] Q,
  output C
);

  wire or_1_out;
  wire [3:0] adder_1_out;

  Register #(.width(4)) register_1 (.D(adder_1_out), .en(WE), .clk(CLK), .Q(Q), .clr(or_1_out));
  Adder #(.width(4)) adder_1 (.a(Q), .b(4'b0001), .out(adder_1_out));  // open: cin, cout
  or or_1 (or_1_out, R, C);
  Comparator #(.mode("unsigned"), .width(4)) comparator_1 (.a(Q), .b(4'b1010), .eq(C));  // open: gt, lt
endmodule
