// Logisim project F3_Half_adderAFull_adder.circ as structural Verilog: 1 circuit, main circuit main
module main (
  input  A0,
  input  B0,
  input  C1,
  input  A1,
  input  B1,
  input  Ci,
  input  Ai,
  input  Bi,
  output S0,
  output C0,
  output CO,
  output SO,
  output S,
  output C
);

  wire and_2_out, and_3_out, and_4_out, and_5_out, and_6_out, and_7_out, and_8_out, and_9_out, and_10_out,
       and_11_out, and_12_out, and_13_out, and_14_out, not_1_out, not_2_out, not_3_out, or_1_out, or_3_out,
       or_4_out, xor_2_out;

  not not_1 (not_1_out, C1);
  not not_2 (not_2_out, A1);
  not not_3 (not_3_out, B1);
  xor xor_1 (S0, A0, B0);
  and and_1 (C0, A0, B0);
  and and_2 (and_2_out, B1, A1);
  xor xor_2 (xor_2_out, Ai, Bi);
  and and_3 (and_3_out, Ai, Bi);
  and and_4 (and_4_out, C1, A1);
  and and_5 (and_5_out, A1, B1);
  and and_6 (and_6_out, C1, B1);
  and and_7 (and_7_out, not_2_out, not_3_out);
  and and_8 (and_8_out, not_1_out, not_2_out);
  and and_9 (and_9_out, not_3_out, not_1_out);
  or or_1 (or_1_out, and_4_out, and_5_out);
  and and_10 (and_10_out, C1, and_7_out);
  and and_11 (and_11_out, and_8_out, B1);
  and and_12 (and_12_out, and_9_out, A1);
  and and_13 (and_13_out, and_2_out, C1);
  xor xor_3 (S, Ci, xor_2_out);
  and and_14 (and_14_out, Ci, xor_2_out);
  or or_2 (CO, or_1_out, and_6_out);
  or or_3 (or_3_out, and_10_out, and_11_out);
  or or_4 (or_4_out, and_12_out, and_13_out);
  or or_5 (C, and_14_out, and_3_out);
  or or_6 (SO, or_3_out, or_4_out);
endmodule
