// Logisim project F3_Sequence_summation_circuit.circ as structural Verilog: 1 circuit, main circuit main
module main (
  input  WE,
  output [7:0] out_2
);

  wire CLK_out, R_out;
  wire [7:0] adder_1_out, adder_2_out, register_1_q;

  Adder adder_1 (.a(register_1_q), .b(8'h1), .out(adder_1_out));  // open: cin, cout
  Button CLK (.out(CLK_out));
  Button R (.out(R_out));
  Register register_1 (.D(adder_1_out), .en(WE), .clk(CLK_out), .Q(register_1_q), .clr(R_out));
  Adder adder_2 (.a(out_2), .b(register_1_q), .out(adder_2_out));  // open: cin, cout
  Register register_2 (.D(adder_2_out), .en(WE), .clk(CLK_out), .Q(out_2), .clr(R_out));
endmodule
