// Logisim project F5_Implement_outrs_function.circ as structural Verilog: 6 circuits, main circuit main
module main (
  input  WE,
  input  [1:0] in_2,
  output [7:0] out_3
);

  wire add, and_1_out, bner0, branch, button_1_out, clock_1_out, clock_2_out, comparator_1_eq, li, not_1_out,
       not_2_out, not_3_out, not_4_out, or_1_out, outrs;
  wire [1:0] multiplexer_2_out, multiplexer_3_out;
  wire [2:0] adder_1_out, multiplexer_1_out, register_1_q;
  wire [5:0] ARGS;
  wire [7:0] ssd, two_port_gpr_1_rdata1, two_port_gpr_1_rdata2, two_port_gpr_1_rdata3, wdata;
  wire [7:6] pc_sum_1_cmd;

  Multiplexer #(.width(3)) multiplexer_1 (.in0(adder_1_out), .in1(ARGS[4:2]), .out(multiplexer_1_out), .sel(branch));
  Adder #(.width(3)) adder_1 (.a(register_1_q), .b(3'b001), .out(adder_1_out));  // open: cin, cout
  Clock clock_1 (.out(clock_1_out));
  Button button_1 (.out(button_1_out));
  not not_1 (not_1_out, bner0);
  not not_2 (not_2_out, outrs);
  or or_1 (or_1_out, li, add);
  Clock clock_2 (.out(clock_2_out));
  Multiplexer #(.width(2)) multiplexer_2 (.in0(ARGS[3:2]), .in1(2'b00), .out(multiplexer_2_out), .sel(bner0));
  Multiplexer #(.width(2)) multiplexer_3 (
    .in0(multiplexer_2_out), .in1(ARGS[1:0]), .out(multiplexer_3_out), .sel(outrs));
  Register #(.width(3)) register_1 (
    .D(multiplexer_1_out), .en(WE), .clk(clock_1_out), .Q(register_1_q), .clr(button_1_out));
  and and_1 (and_1_out, not_1_out, not_2_out, or_1_out);
  // Probe on register_1_q
  Decoder #(.enable("false"), .select(2)) decoder_1 (
    .out0(add), .out1(outrs), .out2(li), .out3(bner0), .sel(pc_sum_1_cmd));
  Multiplexer #(.width(8)) multiplexer_4 (.in0(out_3), .in1({4'b0000, ARGS[3:0]}), .out(wdata), .sel(not_3_out));
  not not_3 (not_3_out, add);
  PC_SUM pc_sum_1 (.ADDR(register_1_q), .CMD({pc_sum_1_cmd, ARGS}));
  // Probe on two_port_gpr_1_rdata3
  two_port_GPR two_port_gpr_1 (
    .wdata(wdata), .raddr3(in_2), .waddr(ARGS[5:4]), .wen(and_1_out), .CLK(clock_2_out),
    .raddr1(multiplexer_3_out), .raddr2(ARGS[1:0]), .rdata3(two_port_gpr_1_rdata3),
    .rdata1(two_port_gpr_1_rdata1), .rdata2(two_port_gpr_1_rdata2));
  // Probe on pc_sum_1_cmd
  Hex_Digit_Display hex_digit_display_1 (.value(ssd[7:4]));  // open: dp
  Hex_Digit_Display hex_digit_display_2 (.value(ssd[3:0]));  // open: dp
  Multiplexer #(.width(8)) multiplexer_5 (.in0({8{1'b0}}), .in1(two_port_gpr_1_rdata1), .out(ssd), .sel(outrs));
  Adder adder_2 (.a(two_port_gpr_1_rdata1), .b(two_port_gpr_1_rdata2), .out(out_3));  // open: cin, cout
  Comparator comparator_1 (.a(two_port_gpr_1_rdata1), .b(two_port_gpr_1_rdata2), .eq(comparator_1_eq));  // open: gt, lt
  not not_4 (not_4_out, comparator_1_eq);
  and and_2 (branch, not_4_out, bner0);

  // Other names for the same wires on the sheet: waddr[1:0] = ARGS[5:4]; PLUSOUT[7:0] = out_3
endmodule

module PC_SUM (
  input  [2:0] ADDR,
  output [7:0] CMD
);

  wire and_1_out, and_2_out, and_3_out, and_4_out, and_5_out, and_6_out, and_7_out, and_8_out, and_9_out,
       and_10_out, and_11_out, and_12_out, and_13_out, and_14_out, and_15_out, and_16_out, and_17_out,
       and_18_out, and_19_out, and_20_out, and_21_out, and_22_out, and_23_out, and_24_out, and_25_out,
       and_26_out, and_27_out, and_28_out, and_29_out, and_30_out, and_31_out, and_32_out, and_33_out,
       and_34_out, and_35_out, and_36_out, and_37_out, and_38_out, and_39_out, and_40_out, and_41_out,
       and_42_out, and_43_out, and_44_out, and_45_out, and_46_out, and_47_out, and_48_out, and_49_out,
       and_50_out, and_51_out, and_52_out, and_53_out, and_54_out, and_55_out, and_56_out, and_57_out,
       and_58_out, and_59_out, and_60_out, and_61_out, and_62_out, and_63_out, and_64_out, decoder_1_out0,
       decoder_1_out1, decoder_1_out2, decoder_1_out3, decoder_1_out4, decoder_1_out5, decoder_1_out6,
       decoder_1_out7;

  Decoder #(.enable("false"), .select(3)) decoder_1 (
    .out0(decoder_1_out0), .out1(decoder_1_out1), .out2(decoder_1_out2), .out3(decoder_1_out3),
    .out4(decoder_1_out4), .out5(decoder_1_out5), .out6(decoder_1_out6), .out7(decoder_1_out7), .sel(ADDR));
  and and_1 (and_1_out, decoder_1_out0, 1'b1);
  and and_2 (and_2_out, decoder_1_out1, 1'b1);
  and and_3 (and_3_out, decoder_1_out2, 1'b1);
  and and_4 (and_4_out, decoder_1_out3, 1'b1);
  and and_5 (and_5_out, decoder_1_out4, 1'b0);
  and and_6 (and_6_out, decoder_1_out5, 1'b0);
  and and_7 (and_7_out, decoder_1_out6, 1'b1);
  and and_8 (and_8_out, decoder_1_out7, 1'b0);
  or or_1 (CMD[7], and_8_out, and_7_out, and_6_out, and_5_out, and_4_out, and_3_out, and_2_out, and_1_out);
  and and_9 (and_9_out, decoder_1_out0, 1'b0);
  and and_10 (and_10_out, decoder_1_out1, 1'b0);
  and and_11 (and_11_out, decoder_1_out2, 1'b0);
  and and_12 (and_12_out, decoder_1_out3, 1'b0);
  and and_13 (and_13_out, decoder_1_out4, 1'b0);
  and and_14 (and_14_out, decoder_1_out5, 1'b0);
  and and_15 (and_15_out, decoder_1_out6, 1'b1);
  and and_16 (and_16_out, decoder_1_out7, 1'b1);
  or or_2 (CMD[6], and_16_out, and_15_out, and_14_out, and_13_out, and_12_out, and_11_out, and_10_out, and_9_out);
  and and_17 (and_17_out, decoder_1_out0, 1'b0);
  and and_18 (and_18_out, decoder_1_out1, 1'b0);
  and and_19 (and_19_out, decoder_1_out2, 1'b1);
  and and_20 (and_20_out, decoder_1_out3, 1'b1);
  and and_21 (and_21_out, decoder_1_out4, 1'b0);
  and and_22 (and_22_out, decoder_1_out5, 1'b1);
  and and_23 (and_23_out, decoder_1_out6, 1'b0);
  and and_24 (and_24_out, decoder_1_out7, 1'b0);
  or or_3 (CMD[5], and_24_out, and_23_out, and_22_out, and_21_out, and_20_out, and_19_out, and_18_out, and_17_out);
  and and_25 (and_25_out, decoder_1_out0, 1'b0);
  and and_26 (and_26_out, decoder_1_out1, 1'b1);
  and and_27 (and_27_out, decoder_1_out2, 1'b0);
  and and_28 (and_28_out, decoder_1_out3, 1'b1);
  and and_29 (and_29_out, decoder_1_out4, 1'b1);
  and and_30 (and_30_out, decoder_1_out5, 1'b0);
  and and_31 (and_31_out, decoder_1_out6, 1'b1);
  and and_32 (and_32_out, decoder_1_out7, 1'b0);
  or or_4 (CMD[4], and_32_out, and_31_out, and_30_out, and_29_out, and_28_out, and_27_out, and_26_out, and_25_out);
  and and_33 (and_33_out, decoder_1_out0, 1'b1);
  and and_34 (and_34_out, decoder_1_out1, 1'b0);
  and and_35 (and_35_out, decoder_1_out2, 1'b0);
  and and_36 (and_36_out, decoder_1_out3, 1'b0);
  and and_37 (and_37_out, decoder_1_out4, 1'b0);
  and and_38 (and_38_out, decoder_1_out5, 1'b1);
  and and_39 (and_39_out, decoder_1_out6, 1'b0);
  and and_40 (and_40_out, decoder_1_out7, 1'b0);
  or or_5 (CMD[3], and_40_out, and_39_out, and_38_out, and_37_out, and_36_out, and_35_out, and_34_out, and_33_out);
  and and_41 (and_41_out, decoder_1_out0, 1'b0);
  and and_42 (and_42_out, decoder_1_out1, 1'b0);
  and and_43 (and_43_out, decoder_1_out2, 1'b0);
  and and_44 (and_44_out, decoder_1_out3, 1'b0);
  and and_45 (and_45_out, decoder_1_out4, 1'b1);
  and and_46 (and_46_out, decoder_1_out5, 1'b0);
  and and_47 (and_47_out, decoder_1_out6, 1'b0);
  and and_48 (and_48_out, decoder_1_out7, 1'b0);
  or or_6 (CMD[2], and_48_out, and_47_out, and_46_out, and_45_out, and_44_out, and_43_out, and_42_out, and_41_out);
  and and_49 (and_49_out, decoder_1_out0, 1'b1);
  and and_50 (and_50_out, decoder_1_out1, 1'b0);
  and and_51 (and_51_out, decoder_1_out2, 1'b0);
  and and_52 (and_52_out, decoder_1_out3, 1'b0);
  and and_53 (and_53_out, decoder_1_out4, 1'b1);
  and and_54 (and_54_out, decoder_1_out5, 1'b0);
  and and_55 (and_55_out, decoder_1_out6, 1'b0);
  and and_56 (and_56_out, decoder_1_out7, 1'b1);
  or or_7 (CMD[1], and_56_out, and_55_out, and_54_out, and_53_out, and_52_out, and_51_out, and_50_out, and_49_out);
  and and_57 (and_57_out, decoder_1_out0, 1'b0);
  and and_58 (and_58_out, decoder_1_out1, 1'b0);
  and and_59 (and_59_out, decoder_1_out2, 1'b0);
  and and_60 (and_60_out, decoder_1_out3, 1'b1);
  and and_61 (and_61_out, decoder_1_out4, 1'b1);
  and and_62 (and_62_out, decoder_1_out5, 1'b1);
  and and_63 (and_63_out, decoder_1_out6, 1'b1);
  and and_64 (and_64_out, decoder_1_out7, 1'b0);
  or or_8 (CMD[0], and_64_out, and_63_out, and_62_out, and_61_out, and_60_out, and_59_out, and_58_out, and_57_out);
endmodule

module GPR (
  input  [7:0] D,
  input  [1:0] ADDR1,
  input  EN,
  input  CLK,
  output [7:0] Q
);

  wire and_1_out, and_2_out, and_3_out, and_4_out, and_5_out, and_6_out, and_7_out, and_8_out, and_9_out,
       and_10_out, and_11_out, and_12_out, and_13_out, and_14_out, and_15_out, and_16_out, and_17_out,
       and_18_out, and_19_out, and_20_out, and_21_out, and_22_out, and_23_out, and_24_out, and_25_out,
       and_26_out, and_27_out, and_28_out, and_29_out, and_30_out, and_31_out, and_32_out, and_33_out,
       and_34_out, and_35_out, and_36_out, decoder_1_out0, decoder_1_out1, decoder_1_out2, decoder_1_out3,
       dffwen_1_q, dffwen_2_q, dffwen_3_q, dffwen_4_q, dffwen_5_q, dffwen_6_q, dffwen_7_q, dffwen_8_q,
       dffwen_9_q, dffwen_10_q, dffwen_11_q, dffwen_12_q, dffwen_13_q, dffwen_14_q, dffwen_15_q, dffwen_16_q,
       dffwen_17_q, dffwen_18_q, dffwen_19_q, dffwen_20_q, dffwen_21_q, dffwen_22_q, dffwen_23_q,
       dffwen_24_q, dffwen_25_q, dffwen_26_q, dffwen_27_q, dffwen_28_q, dffwen_29_q, dffwen_30_q,
       dffwen_31_q, dffwen_32_q;

  Decoder #(.enable("false"), .select(2)) decoder_1 (
    .out0(decoder_1_out0), .out1(decoder_1_out1), .out2(decoder_1_out2), .out3(decoder_1_out3), .sel(ADDR1));
  and and_1 (and_1_out, decoder_1_out0, EN);
  and and_2 (and_2_out, decoder_1_out1, EN);
  and and_3 (and_3_out, decoder_1_out2, EN);
  and and_4 (and_4_out, decoder_1_out3, EN);
  DFFWEN dffwen_1 (.D(D[7]), .EN(and_1_out), .CLK(CLK), .Q(dffwen_1_q));
  DFFWEN dffwen_2 (.D(D[7]), .EN(and_2_out), .CLK(CLK), .Q(dffwen_2_q));
  DFFWEN dffwen_3 (.D(D[7]), .EN(and_3_out), .CLK(CLK), .Q(dffwen_3_q));
  DFFWEN dffwen_4 (.D(D[7]), .EN(and_4_out), .CLK(CLK), .Q(dffwen_4_q));
  and and_5 (and_5_out, decoder_1_out0, dffwen_1_q);
  and and_6 (and_6_out, decoder_1_out1, dffwen_2_q);
  and and_7 (and_7_out, decoder_1_out2, dffwen_3_q);
  and and_8 (and_8_out, decoder_1_out3, dffwen_4_q);
  or or_1 (Q[7], and_8_out, and_7_out, and_6_out, and_5_out);
  and and_9 (and_9_out, decoder_1_out0, dffwen_5_q);
  DFFWEN dffwen_5 (.D(D[6]), .EN(and_1_out), .CLK(CLK), .Q(dffwen_5_q));
  and and_10 (and_10_out, decoder_1_out1, dffwen_6_q);
  DFFWEN dffwen_6 (.D(D[6]), .EN(and_2_out), .CLK(CLK), .Q(dffwen_6_q));
  and and_11 (and_11_out, decoder_1_out2, dffwen_7_q);
  DFFWEN dffwen_7 (.D(D[6]), .EN(and_3_out), .CLK(CLK), .Q(dffwen_7_q));
  and and_12 (and_12_out, decoder_1_out3, dffwen_8_q);
  DFFWEN dffwen_8 (.D(D[6]), .EN(and_4_out), .CLK(CLK), .Q(dffwen_8_q));
  or or_2 (Q[6], and_12_out, and_11_out, and_10_out, and_9_out);
  DFFWEN dffwen_9 (.D(D[5]), .EN(and_1_out), .CLK(CLK), .Q(dffwen_9_q));
  DFFWEN dffwen_10 (.D(D[5]), .EN(and_2_out), .CLK(CLK), .Q(dffwen_10_q));
  DFFWEN dffwen_11 (.D(D[5]), .EN(and_3_out), .CLK(CLK), .Q(dffwen_11_q));
  DFFWEN dffwen_12 (.D(D[5]), .EN(and_4_out), .CLK(CLK), .Q(dffwen_12_q));
  and and_13 (and_13_out, decoder_1_out0, dffwen_9_q);
  and and_14 (and_14_out, decoder_1_out1, dffwen_10_q);
  and and_15 (and_15_out, decoder_1_out2, dffwen_11_q);
  and and_16 (and_16_out, decoder_1_out3, dffwen_12_q);
  or or_3 (Q[5], and_16_out, and_15_out, and_14_out, and_13_out);
  and and_17 (and_17_out, decoder_1_out0, dffwen_13_q);
  DFFWEN dffwen_13 (.D(D[4]), .EN(and_1_out), .CLK(CLK), .Q(dffwen_13_q));
  and and_18 (and_18_out, decoder_1_out1, dffwen_14_q);
  DFFWEN dffwen_14 (.D(D[4]), .EN(and_2_out), .CLK(CLK), .Q(dffwen_14_q));
  and and_19 (and_19_out, decoder_1_out2, dffwen_15_q);
  DFFWEN dffwen_15 (.D(D[4]), .EN(and_3_out), .CLK(CLK), .Q(dffwen_15_q));
  and and_20 (and_20_out, decoder_1_out3, dffwen_16_q);
  DFFWEN dffwen_16 (.D(D[4]), .EN(and_4_out), .CLK(CLK), .Q(dffwen_16_q));
  or or_4 (Q[4], and_17_out, and_20_out, and_18_out, and_19_out);
  and and_21 (and_21_out, decoder_1_out0, dffwen_17_q);
  DFFWEN dffwen_17 (.D(D[3]), .EN(and_1_out), .CLK(CLK), .Q(dffwen_17_q));
  and and_22 (and_22_out, decoder_1_out1, dffwen_18_q);
  DFFWEN dffwen_18 (.D(D[3]), .EN(and_2_out), .CLK(CLK), .Q(dffwen_18_q));
  and and_23 (and_23_out, decoder_1_out2, dffwen_19_q);
  DFFWEN dffwen_19 (.D(D[3]), .EN(and_3_out), .CLK(CLK), .Q(dffwen_19_q));
  and and_24 (and_24_out, decoder_1_out3, dffwen_20_q);
  DFFWEN dffwen_20 (.D(D[3]), .EN(and_4_out), .CLK(CLK), .Q(dffwen_20_q));
  or or_5 (Q[3], and_24_out, and_23_out, and_22_out, and_21_out);
  DFFWEN dffwen_21 (.D(D[2]), .EN(and_1_out), .CLK(CLK), .Q(dffwen_21_q));
  DFFWEN dffwen_22 (.D(D[2]), .EN(and_2_out), .CLK(CLK), .Q(dffwen_22_q));
  DFFWEN dffwen_23 (.D(D[2]), .EN(and_3_out), .CLK(CLK), .Q(dffwen_23_q));
  DFFWEN dffwen_24 (.D(D[2]), .EN(and_4_out), .CLK(CLK), .Q(dffwen_24_q));
  and and_25 (and_25_out, decoder_1_out0, dffwen_21_q);
  and and_26 (and_26_out, decoder_1_out1, dffwen_22_q);
  and and_27 (and_27_out, decoder_1_out2, dffwen_23_q);
  and and_28 (and_28_out, decoder_1_out3, dffwen_24_q);
  or or_6 (Q[2], and_28_out, and_27_out, and_26_out, and_25_out);
  DFFWEN dffwen_25 (.D(D[1]), .EN(and_1_out), .CLK(CLK), .Q(dffwen_25_q));
  DFFWEN dffwen_26 (.D(D[1]), .EN(and_2_out), .CLK(CLK), .Q(dffwen_26_q));
  DFFWEN dffwen_27 (.D(D[1]), .EN(and_3_out), .CLK(CLK), .Q(dffwen_27_q));
  DFFWEN dffwen_28 (.D(D[1]), .EN(and_4_out), .CLK(CLK), .Q(dffwen_28_q));
  and and_29 (and_29_out, decoder_1_out0, dffwen_25_q);
  and and_30 (and_30_out, decoder_1_out1, dffwen_26_q);
  and and_31 (and_31_out, decoder_1_out2, dffwen_27_q);
  and and_32 (and_32_out, decoder_1_out3, dffwen_28_q);
  or or_7 (Q[1], and_32_out, and_31_out, and_30_out, and_29_out);
  DFFWEN dffwen_29 (.D(D[0]), .EN(and_1_out), .CLK(CLK), .Q(dffwen_29_q));
  DFFWEN dffwen_30 (.D(D[0]), .EN(and_2_out), .CLK(CLK), .Q(dffwen_30_q));
  DFFWEN dffwen_31 (.D(D[0]), .EN(and_3_out), .CLK(CLK), .Q(dffwen_31_q));
  DFFWEN dffwen_32 (.D(D[0]), .EN(and_4_out), .CLK(CLK), .Q(dffwen_32_q));
  and and_33 (and_33_out, decoder_1_out0, dffwen_29_q);
  and and_34 (and_34_out, decoder_1_out1, dffwen_30_q);
  and and_35 (and_35_out, decoder_1_out2, dffwen_31_q);
  and and_36 (and_36_out, decoder_1_out3, dffwen_32_q);
  or or_8 (Q[0], and_36_out, and_35_out, and_34_out, and_33_out);
endmodule

module DFFWEN (
  input  D,
  input  EN,
  input  CLK,
  output Q
);

  wire multiplexer_1_out;

  D_Flip_Flop d_ff_1 (.D(multiplexer_1_out), .clk(CLK), .Q(Q));  // open: Qn, preset, reset
  Multiplexer multiplexer_1 (.in0(Q), .in1(D), .out(multiplexer_1_out), .sel(EN));
endmodule

module two_port_GPR (
  input  [7:0] wdata,
  input  [1:0] raddr3,
  input  [1:0] waddr,
  input  wen,
  input  CLK,
  input  [1:0] raddr1,
  input  [1:0] raddr2,
  output [7:0] rdata3,
  output [7:0] rdata1,
  output [7:0] rdata2
);

  wire and_1_out, and_2_out, and_3_out, and_4_out, and_5_out, and_6_out, and_7_out, and_8_out, and_9_out,
       and_10_out, and_11_out, and_12_out, and_13_out, and_14_out, and_15_out, and_16_out, and_17_out,
       and_18_out, and_19_out, and_20_out, and_21_out, and_22_out, and_23_out, and_24_out, and_25_out,
       and_26_out, and_27_out, and_28_out, and_29_out, and_30_out, and_31_out, and_32_out, and_33_out,
       and_34_out, and_35_out, and_36_out, and_37_out, and_38_out, and_39_out, and_40_out, and_41_out,
       and_42_out, and_43_out, and_44_out, and_45_out, and_46_out, and_47_out, and_48_out, and_49_out,
       and_50_out, and_51_out, and_52_out, and_53_out, and_54_out, and_55_out, and_56_out, and_57_out,
       and_58_out, and_59_out, and_60_out, and_61_out, and_62_out, and_63_out, and_64_out, and_65_out,
       and_66_out, and_67_out, and_68_out, and_69_out, and_70_out, and_71_out, and_72_out, and_73_out,
       and_74_out, and_75_out, and_76_out, and_77_out, and_78_out, and_79_out, and_80_out, and_81_out,
       and_82_out, and_83_out, and_84_out, and_85_out, and_86_out, and_87_out, and_88_out, and_89_out,
       and_90_out, and_91_out, and_92_out, and_93_out, and_94_out, and_95_out, and_96_out, and_97_out,
       and_98_out, and_99_out, and_100_out, b00, b01, b02, b03, b04, b05, b06, b07, b10, b11, b12, b13, b14,
       b15, b16, b17, b20, b21, b22, b23, b24, b25, b26, b27, b30, b31, b32, b33, b34, b35, b36, b37,
       decoder_1_out0, decoder_1_out1, decoder_1_out2, decoder_1_out3, decoder_3_out0, decoder_3_out1,
       decoder_3_out2, decoder_3_out3, decoder_4_out0, decoder_4_out1, decoder_4_out2, decoder_4_out3,
       R1_WL0, R1_WL1, R1_WL2, R1_WL3;

  Decoder #(.enable("false"), .select(2)) decoder_1 (
    .out0(decoder_1_out0), .out1(decoder_1_out1), .out2(decoder_1_out2), .out3(decoder_1_out3), .sel(raddr2));
  Decoder #(.enable("false"), .select(2)) decoder_2 (
    .out0(R1_WL0), .out1(R1_WL1), .out2(R1_WL2), .out3(R1_WL3), .sel(raddr1));
  Decoder #(.enable("false"), .select(2)) decoder_3 (
    .out0(decoder_3_out0), .out1(decoder_3_out1), .out2(decoder_3_out2), .out3(decoder_3_out3), .sel(waddr));
  and and_1 (and_1_out, decoder_3_out0, wen);
  and and_2 (and_2_out, decoder_3_out1, wen);
  and and_3 (and_3_out, decoder_3_out2, wen);
  and and_4 (and_4_out, decoder_3_out3, wen);
  DFFWEN dffwen_1 (.D(wdata[7]), .EN(and_1_out), .CLK(CLK), .Q(b07));
  DFFWEN dffwen_2 (.D(wdata[7]), .EN(and_2_out), .CLK(CLK), .Q(b17));
  DFFWEN dffwen_3 (.D(wdata[7]), .EN(and_3_out), .CLK(CLK), .Q(b27));
  DFFWEN dffwen_4 (.D(wdata[7]), .EN(and_4_out), .CLK(CLK), .Q(b37));
  and and_5 (and_5_out, decoder_1_out0, b07);
  and and_6 (and_6_out, decoder_1_out1, b17);
  and and_7 (and_7_out, decoder_1_out2, b27);
  and and_8 (and_8_out, decoder_1_out3, b37);
  or or_1 (rdata2[7], and_8_out, and_7_out, and_6_out, and_5_out);
  and and_9 (and_9_out, R1_WL0, b07);
  and and_10 (and_10_out, R1_WL1, b17);
  and and_11 (and_11_out, R1_WL2, b27);
  and and_12 (and_12_out, R1_WL3, b37);
  or or_2 (rdata1[7], and_12_out, and_11_out, and_10_out, and_9_out);
  and and_13 (and_13_out, decoder_1_out0, b06);
  and and_14 (and_14_out, decoder_1_out1, b16);
  and and_15 (and_15_out, decoder_1_out2, b26);
  and and_16 (and_16_out, decoder_1_out3, b36);
  or or_3 (rdata2[6], and_16_out, and_15_out, and_14_out, and_13_out);
  and and_17 (and_17_out, R1_WL0, b06);
  DFFWEN dffwen_5 (.D(wdata[6]), .EN(and_1_out), .CLK(CLK), .Q(b06));
  and and_18 (and_18_out, R1_WL1, b16);
  DFFWEN dffwen_6 (.D(wdata[6]), .EN(and_2_out), .CLK(CLK), .Q(b16));
  and and_19 (and_19_out, R1_WL2, b26);
  DFFWEN dffwen_7 (.D(wdata[6]), .EN(and_3_out), .CLK(CLK), .Q(b26));
  and and_20 (and_20_out, R1_WL3, b36);
  DFFWEN dffwen_8 (.D(wdata[6]), .EN(and_4_out), .CLK(CLK), .Q(b36));
  or or_4 (rdata1[6], and_20_out, and_19_out, and_18_out, and_17_out);
  and and_21 (and_21_out, decoder_1_out0, b05);
  and and_22 (and_22_out, decoder_1_out1, b15);
  and and_23 (and_23_out, decoder_1_out2, b25);
  and and_24 (and_24_out, decoder_1_out3, b35);
  DFFWEN dffwen_9 (.D(wdata[5]), .EN(and_1_out), .CLK(CLK), .Q(b05));
  DFFWEN dffwen_10 (.D(wdata[5]), .EN(and_2_out), .CLK(CLK), .Q(b15));
  DFFWEN dffwen_11 (.D(wdata[5]), .EN(and_3_out), .CLK(CLK), .Q(b25));
  DFFWEN dffwen_12 (.D(wdata[5]), .EN(and_4_out), .CLK(CLK), .Q(b35));
  or or_5 (rdata2[5], and_24_out, and_23_out, and_22_out, and_21_out);
  and and_25 (and_25_out, R1_WL0, b05);
  and and_26 (and_26_out, R1_WL1, b15);
  and and_27 (and_27_out, R1_WL2, b25);
  and and_28 (and_28_out, R1_WL3, b35);
  or or_6 (rdata1[5], and_28_out, and_27_out, and_26_out, and_25_out);
  and and_29 (and_29_out, decoder_1_out0, b04);
  and and_30 (and_30_out, decoder_1_out1, b14);
  and and_31 (and_31_out, decoder_1_out2, b24);
  and and_32 (and_32_out, decoder_1_out3, b34);
  or or_7 (rdata2[4], and_32_out, and_31_out, and_30_out, and_29_out);
  and and_33 (and_33_out, R1_WL0, b04);
  DFFWEN dffwen_13 (.D(wdata[4]), .EN(and_1_out), .CLK(CLK), .Q(b04));
  and and_34 (and_34_out, R1_WL1, b14);
  DFFWEN dffwen_14 (.D(wdata[4]), .EN(and_2_out), .CLK(CLK), .Q(b14));
  and and_35 (and_35_out, R1_WL2, b24);
  DFFWEN dffwen_15 (.D(wdata[4]), .EN(and_3_out), .CLK(CLK), .Q(b24));
  and and_36 (and_36_out, R1_WL3, b34);
  DFFWEN dffwen_16 (.D(wdata[4]), .EN(and_4_out), .CLK(CLK), .Q(b34));
  or or_8 (rdata1[4], and_33_out, and_36_out, and_34_out, and_35_out);
  and and_37 (and_37_out, decoder_1_out0, b03);
  and and_38 (and_38_out, decoder_1_out1, b13);
  and and_39 (and_39_out, decoder_1_out2, b23);
  and and_40 (and_40_out, decoder_1_out3, b33);
  or or_9 (rdata2[3], and_40_out, and_39_out, and_38_out, and_37_out);
  and and_41 (and_41_out, R1_WL0, b03);
  DFFWEN dffwen_17 (.D(wdata[3]), .EN(and_1_out), .CLK(CLK), .Q(b03));
  and and_42 (and_42_out, R1_WL1, b13);
  DFFWEN dffwen_18 (.D(wdata[3]), .EN(and_2_out), .CLK(CLK), .Q(b13));
  and and_43 (and_43_out, R1_WL2, b23);
  DFFWEN dffwen_19 (.D(wdata[3]), .EN(and_3_out), .CLK(CLK), .Q(b23));
  and and_44 (and_44_out, R1_WL3, b33);
  DFFWEN dffwen_20 (.D(wdata[3]), .EN(and_4_out), .CLK(CLK), .Q(b33));
  or or_10 (rdata1[3], and_44_out, and_43_out, and_42_out, and_41_out);
  and and_45 (and_45_out, decoder_1_out0, b02);
  and and_46 (and_46_out, decoder_1_out1, b12);
  and and_47 (and_47_out, decoder_1_out2, b22);
  and and_48 (and_48_out, decoder_1_out3, b32);
  or or_11 (rdata2[2], and_48_out, and_47_out, and_46_out, and_45_out);
  DFFWEN dffwen_21 (.D(wdata[2]), .EN(and_1_out), .CLK(CLK), .Q(b02));
  DFFWEN dffwen_22 (.D(wdata[2]), .EN(and_2_out), .CLK(CLK), .Q(b12));
  DFFWEN dffwen_23 (.D(wdata[2]), .EN(and_3_out), .CLK(CLK), .Q(b22));
  DFFWEN dffwen_24 (.D(wdata[2]), .EN(and_4_out), .CLK(CLK), .Q(b32));
  and and_49 (and_49_out, R1_WL0, b02);
  and and_50 (and_50_out, R1_WL1, b12);
  and and_51 (and_51_out, R1_WL2, b22);
  and and_52 (and_52_out, R1_WL3, b32);
  or or_12 (rdata1[2], and_52_out, and_51_out, and_50_out, and_49_out);
  and and_53 (and_53_out, decoder_1_out0, b01);
  and and_54 (and_54_out, decoder_1_out1, b11);
  and and_55 (and_55_out, decoder_1_out2, b21);
  and and_56 (and_56_out, decoder_1_out3, b31);
  DFFWEN dffwen_25 (.D(wdata[1]), .EN(and_1_out), .CLK(CLK), .Q(b01));
  DFFWEN dffwen_26 (.D(wdata[1]), .EN(and_2_out), .CLK(CLK), .Q(b11));
  DFFWEN dffwen_27 (.D(wdata[1]), .EN(and_3_out), .CLK(CLK), .Q(b21));
  DFFWEN dffwen_28 (.D(wdata[1]), .EN(and_4_out), .CLK(CLK), .Q(b31));
  or or_13 (rdata2[1], and_56_out, and_55_out, and_54_out, and_53_out);
  and and_57 (and_57_out, R1_WL0, b01);
  and and_58 (and_58_out, R1_WL1, b11);
  and and_59 (and_59_out, R1_WL2, b21);
  and and_60 (and_60_out, R1_WL3, b31);
  or or_14 (rdata1[1], and_60_out, and_59_out, and_58_out, and_57_out);
  and and_61 (and_61_out, decoder_1_out0, b00);
  and and_62 (and_62_out, decoder_1_out1, b10);
  and and_63 (and_63_out, decoder_1_out2, b20);
  and and_64 (and_64_out, decoder_1_out3, b30);
  DFFWEN dffwen_29 (.D(wdata[0]), .EN(and_1_out), .CLK(CLK), .Q(b00));
  DFFWEN dffwen_30 (.D(wdata[0]), .EN(and_2_out), .CLK(CLK), .Q(b10));
  DFFWEN dffwen_31 (.D(wdata[0]), .EN(and_3_out), .CLK(CLK), .Q(b20));
  DFFWEN dffwen_32 (.D(wdata[0]), .EN(and_4_out), .CLK(CLK), .Q(b30));
  or or_15 (rdata2[0], and_64_out, and_63_out, and_62_out, and_61_out);
  and and_65 (and_65_out, R1_WL0, b00);
  and and_66 (and_66_out, R1_WL1, b10);
  and and_67 (and_67_out, R1_WL2, b20);
  and and_68 (and_68_out, R1_WL3, b30);
  or or_16 (rdata1[0], and_68_out, and_67_out, and_66_out, and_65_out);
  Decoder #(.enable("false"), .select(2)) decoder_4 (
    .out0(decoder_4_out0), .out1(decoder_4_out1), .out2(decoder_4_out2), .out3(decoder_4_out3), .sel(raddr3));
  and and_69 (and_69_out, decoder_4_out0, b07);
  and and_70 (and_70_out, decoder_4_out1, b17);
  and and_71 (and_71_out, decoder_4_out2, b27);
  and and_72 (and_72_out, decoder_4_out3, b37);
  or or_17 (rdata3[7], and_72_out, and_71_out, and_70_out, and_69_out);
  and and_73 (and_73_out, decoder_4_out0, b06);
  and and_74 (and_74_out, decoder_4_out1, b16);
  and and_75 (and_75_out, decoder_4_out2, b26);
  and and_76 (and_76_out, decoder_4_out3, b36);
  or or_18 (rdata3[6], and_76_out, and_75_out, and_74_out, and_73_out);
  and and_77 (and_77_out, decoder_4_out0, b05);
  and and_78 (and_78_out, decoder_4_out1, b15);
  and and_79 (and_79_out, decoder_4_out2, b25);
  and and_80 (and_80_out, decoder_4_out3, b35);
  or or_19 (rdata3[5], and_80_out, and_79_out, and_78_out, and_77_out);
  and and_81 (and_81_out, decoder_4_out0, b04);
  and and_82 (and_82_out, decoder_4_out1, b14);
  and and_83 (and_83_out, decoder_4_out2, b24);
  and and_84 (and_84_out, decoder_4_out3, b34);
  or or_20 (rdata3[4], and_84_out, and_83_out, and_82_out, and_81_out);
  and and_85 (and_85_out, decoder_4_out0, b03);
  and and_86 (and_86_out, decoder_4_out1, b13);
  and and_87 (and_87_out, decoder_4_out2, b23);
  and and_88 (and_88_out, decoder_4_out3, b33);
  or or_21 (rdata3[3], and_88_out, and_87_out, and_86_out, and_85_out);
  and and_89 (and_89_out, decoder_4_out0, b02);
  and and_90 (and_90_out, decoder_4_out1, b12);
  and and_91 (and_91_out, decoder_4_out2, b22);
  and and_92 (and_92_out, decoder_4_out3, b32);
  or or_22 (rdata3[2], and_92_out, and_91_out, and_90_out, and_89_out);
  and and_93 (and_93_out, decoder_4_out0, b01);
  and and_94 (and_94_out, decoder_4_out1, b11);
  and and_95 (and_95_out, decoder_4_out2, b21);
  and and_96 (and_96_out, decoder_4_out3, b31);
  or or_23 (rdata3[1], and_96_out, and_95_out, and_94_out, and_93_out);
  and and_97 (and_97_out, decoder_4_out0, b00);
  and and_98 (and_98_out, decoder_4_out1, b10);
  and and_99 (and_99_out, decoder_4_out2, b20);
  and and_100 (and_100_out, decoder_4_out3, b30);
  or or_24 (rdata3[0], and_100_out, and_99_out, and_98_out, and_97_out);
endmodule

module PC_SUMODDIN10 (
  input  [2:0] ADDR,
  output [7:0] CMD
);

  wire and_1_out, and_2_out, and_3_out, and_4_out, and_5_out, and_6_out, and_7_out, and_8_out, and_9_out,
       and_10_out, and_11_out, and_12_out, and_13_out, and_14_out, and_15_out, and_16_out, and_17_out,
       and_18_out, and_19_out, and_20_out, and_21_out, and_22_out, and_23_out, and_24_out, and_25_out,
       and_26_out, and_27_out, and_28_out, and_29_out, and_30_out, and_31_out, and_32_out, and_33_out,
       and_34_out, and_35_out, and_36_out, and_37_out, and_38_out, and_39_out, and_40_out, and_41_out,
       and_42_out, and_43_out, and_44_out, and_45_out, and_46_out, and_47_out, and_48_out, and_49_out,
       and_50_out, and_51_out, and_52_out, and_53_out, and_54_out, and_55_out, and_56_out, and_57_out,
       and_58_out, and_59_out, and_60_out, and_61_out, and_62_out, and_63_out, and_64_out, decoder_1_out0,
       decoder_1_out1, decoder_1_out2, decoder_1_out3, decoder_1_out4, decoder_1_out5, decoder_1_out6,
       decoder_1_out7;

  Decoder #(.enable("false"), .select(3)) decoder_1 (
    .out0(decoder_1_out0), .out1(decoder_1_out1), .out2(decoder_1_out2), .out3(decoder_1_out3),
    .out4(decoder_1_out4), .out5(decoder_1_out5), .out6(decoder_1_out6), .out7(decoder_1_out7), .sel(ADDR));
  and and_1 (and_1_out, decoder_1_out0, 1'b1);
  and and_2 (and_2_out, decoder_1_out1, 1'b1);
  and and_3 (and_3_out, decoder_1_out2, 1'b1);
  and and_4 (and_4_out, decoder_1_out3, 1'b1);
  and and_5 (and_5_out, decoder_1_out4, 1'b0);
  and and_6 (and_6_out, decoder_1_out5, 1'b0);
  and and_7 (and_7_out, decoder_1_out6, 1'b1);
  and and_8 (and_8_out, decoder_1_out7, 1'b1);
  or or_1 (CMD[7], and_8_out, and_7_out, and_6_out, and_5_out, and_4_out, and_3_out, and_2_out, and_1_out);
  and and_9 (and_9_out, decoder_1_out0, 1'b0);
  and and_10 (and_10_out, decoder_1_out1, 1'b0);
  and and_11 (and_11_out, decoder_1_out2, 1'b0);
  and and_12 (and_12_out, decoder_1_out3, 1'b0);
  and and_13 (and_13_out, decoder_1_out4, 1'b0);
  and and_14 (and_14_out, decoder_1_out5, 1'b0);
  and and_15 (and_15_out, decoder_1_out6, 1'b1);
  and and_16 (and_16_out, decoder_1_out7, 1'b1);
  or or_2 (CMD[6], and_16_out, and_15_out, and_14_out, and_13_out, and_12_out, and_11_out, and_10_out, and_9_out);
  and and_17 (and_17_out, decoder_1_out0, 1'b0);
  and and_18 (and_18_out, decoder_1_out1, 1'b0);
  and and_19 (and_19_out, decoder_1_out2, 1'b1);
  and and_20 (and_20_out, decoder_1_out3, 1'b1);
  and and_21 (and_21_out, decoder_1_out4, 1'b1);
  and and_22 (and_22_out, decoder_1_out5, 1'b0);
  and and_23 (and_23_out, decoder_1_out6, 1'b0);
  and and_24 (and_24_out, decoder_1_out7, 1'b0);
  or or_3 (CMD[5], and_24_out, and_23_out, and_22_out, and_21_out, and_20_out, and_19_out, and_18_out, and_17_out);
  and and_25 (and_25_out, decoder_1_out0, 1'b0);
  and and_26 (and_26_out, decoder_1_out1, 1'b1);
  and and_27 (and_27_out, decoder_1_out2, 1'b0);
  and and_28 (and_28_out, decoder_1_out3, 1'b1);
  and and_29 (and_29_out, decoder_1_out4, 1'b0);
  and and_30 (and_30_out, decoder_1_out5, 1'b1);
  and and_31 (and_31_out, decoder_1_out6, 1'b1);
  and and_32 (and_32_out, decoder_1_out7, 1'b1);
  or or_4 (CMD[4], and_32_out, and_31_out, and_30_out, and_29_out, and_28_out, and_27_out, and_26_out, and_25_out);
  and and_33 (and_33_out, decoder_1_out0, 1'b1);
  and and_34 (and_34_out, decoder_1_out1, 1'b0);
  and and_35 (and_35_out, decoder_1_out2, 1'b0);
  and and_36 (and_36_out, decoder_1_out3, 1'b0);
  and and_37 (and_37_out, decoder_1_out4, 1'b1);
  and and_38 (and_38_out, decoder_1_out5, 1'b0);
  and and_39 (and_39_out, decoder_1_out6, 1'b0);
  and and_40 (and_40_out, decoder_1_out7, 1'b1);
  or or_5 (CMD[3], and_40_out, and_39_out, and_38_out, and_37_out, and_36_out, and_35_out, and_34_out, and_33_out);
  and and_41 (and_41_out, decoder_1_out0, 1'b0);
  and and_42 (and_42_out, decoder_1_out1, 1'b0);
  and and_43 (and_43_out, decoder_1_out2, 1'b0);
  and and_44 (and_44_out, decoder_1_out3, 1'b0);
  and and_45 (and_45_out, decoder_1_out4, 1'b0);
  and and_46 (and_46_out, decoder_1_out5, 1'b1);
  and and_47 (and_47_out, decoder_1_out6, 1'b0);
  and and_48 (and_48_out, decoder_1_out7, 1'b1);
  or or_6 (CMD[2], and_48_out, and_47_out, and_46_out, and_45_out, and_44_out, and_43_out, and_42_out, and_41_out);
  and and_49 (and_49_out, decoder_1_out0, 1'b1);
  and and_50 (and_50_out, decoder_1_out1, 1'b0);
  and and_51 (and_51_out, decoder_1_out2, 1'b0);
  and and_52 (and_52_out, decoder_1_out3, 1'b1);
  and and_53 (and_53_out, decoder_1_out4, 1'b0);
  and and_54 (and_54_out, decoder_1_out5, 1'b1);
  and and_55 (and_55_out, decoder_1_out6, 1'b0);
  and and_56 (and_56_out, decoder_1_out7, 1'b1);
  or or_7 (CMD[1], and_56_out, and_55_out, and_54_out, and_53_out, and_52_out, and_51_out, and_50_out, and_49_out);
  and and_57 (and_57_out, decoder_1_out0, 1'b1);
  and and_58 (and_58_out, decoder_1_out1, 1'b1);
  and and_59 (and_59_out, decoder_1_out2, 1'b0);
  and and_60 (and_60_out, decoder_1_out3, 1'b0);
  and and_61 (and_61_out, decoder_1_out4, 1'b1);
  and and_62 (and_62_out, decoder_1_out5, 1'b1);
  and and_63 (and_63_out, decoder_1_out6, 1'b1);
  and and_64 (and_64_out, decoder_1_out7, 1'b1);
  or or_8 (CMD[0], and_64_out, and_63_out, and_62_out, and_61_out, and_60_out, and_59_out, and_58_out, and_57_out);
endmodule
