// Logisim project F5_Implement_sCPU_supporting_only_li_instruction.circ as structural Verilog: 4 circuits, main circuit main
module main (
  input  WE,
  output [7:0] out_2
);

  wire button_1_out, clock_1_out, clock_2_out, li, or_1_out;
  wire [1:0] buffer_1_out;
  wire [2:0] adder_1_out, register_1_q;
  wire [5:0] ARGS;
  wire [7:6] pc_sum_1_cmd;

  Clock clock_1 (.out(clock_1_out));
  Button button_1 (.out(button_1_out));
  assign buffer_1_out = ARGS[5:4];  // Buffer buffer_1, 2 bits wide
  Clock clock_2 (.out(clock_2_out));
  Register #(.width(3)) register_1 (.D(adder_1_out), .en(WE), .clk(clock_1_out), .Q(register_1_q), .clr(button_1_out));
  Adder #(.width(3)) adder_1 (.a(register_1_q), .b(3'b001), .out(adder_1_out));  // open: cin, cout
  // Probe on buffer_1_out
  buf or_1 (or_1_out, li);  // OR_Gate
  Decoder #(.enable("false"), .select(2)) decoder_1 (.out2(li), .sel(pc_sum_1_cmd));  // open: out0, out1, out3
  PC_SUM pc_sum_1 (.ADDR(register_1_q), .CMD({pc_sum_1_cmd, ARGS}));
  GPR gpr_1 (.D({4'b0000, ARGS[3:0]}), .ADDR1(buffer_1_out), .EN(or_1_out), .CLK(clock_2_out), .Q(out_2));
endmodule

module PC_SUM (
  input  [2:0] ADDR,
  output [7:0] CMD
);

  wire and_1_out, and_2_out, and_3_out, and_4_out, and_5_out, and_6_out, and_7_out, and_8_out, and_9_out,
       and_10_out, and_11_out, and_12_out, and_13_out, and_14_out, and_15_out, and_16_out, and_17_out,
       and_18_out, and_19_out, and_20_out, and_21_out, and_22_out, and_23_out, and_24_out, and_25_out,
       and_26_out, and_27_out, and_28_out, and_29_out, and_30_out, and_31_out, and_32_out, and_33_out,
       and_34_out, and_35_out, and_36_out, and_37_out, and_38_out, and_39_out, and_40_out, and_41_out,
       and_42_out, and_43_out, and_44_out, and_45_out, and_46_out, and_47_out, and_48_out, and_49_out,
       and_50_out, and_51_out, and_52_out, and_53_out, and_54_out, and_55_out, and_56_out, and_57_out,
       and_58_out, and_59_out, and_60_out, and_61_out, and_62_out, and_63_out, and_64_out, decoder_1_out0,
       decoder_1_out1, decoder_1_out2, decoder_1_out3, decoder_1_out4, decoder_1_out5, decoder_1_out6,
       decoder_1_out7;

  Decoder #(.enable("false"), .select(3)) decoder_1 (
    .out0(decoder_1_out0), .out1(decoder_1_out1), .out2(decoder_1_out2), .out3(decoder_1_out3),
    .out4(decoder_1_out4), .out5(decoder_1_out5), .out6(decoder_1_out6), .out7(decoder_1_out7), .sel(ADDR));
  and and_1 (and_1_out, decoder_1_out0, 1'b1);
  and and_2 (and_2_out, decoder_1_out1, 1'b1);
  and and_3 (and_3_out, decoder_1_out2, 1'b1);
  and and_4 (and_4_out, decoder_1_out3, 1'b1);
  and and_5 (and_5_out, decoder_1_out4, 1'b0);
  and and_6 (and_6_out, decoder_1_out5, 1'b0);
  and and_7 (and_7_out, decoder_1_out6, 1'b1);
  and and_8 (and_8_out, decoder_1_out7, 1'b1);
  or or_1 (CMD[7], and_8_out, and_7_out, and_6_out, and_5_out, and_4_out, and_3_out, and_2_out, and_1_out);
  and and_9 (and_9_out, decoder_1_out0, 1'b0);
  and and_10 (and_10_out, decoder_1_out1, 1'b0);
  and and_11 (and_11_out, decoder_1_out2, 1'b0);
  and and_12 (and_12_out, decoder_1_out3, 1'b0);
  buf and_13 (and_13_out, decoder_1_out4);  // AND_Gate
  and and_14 (and_14_out, decoder_1_out5, 1'b0);
  and and_15 (and_15_out, decoder_1_out6, 1'b1);
  and and_16 (and_16_out, decoder_1_out7, 1'b1);
  or or_2 (CMD[6], and_16_out, and_15_out, and_14_out, and_13_out, and_12_out, and_11_out, and_10_out, and_9_out);
  and and_17 (and_17_out, decoder_1_out0, 1'b0);
  and and_18 (and_18_out, decoder_1_out1, 1'b0);
  and and_19 (and_19_out, decoder_1_out2, 1'b1);
  and and_20 (and_20_out, decoder_1_out3, 1'b1);
  and and_21 (and_21_out, decoder_1_out4, 1'b0);
  and and_22 (and_22_out, decoder_1_out5, 1'b1);
  and and_23 (and_23_out, decoder_1_out6, 1'b0);
  and and_24 (and_24_out, decoder_1_out7, 1'b0);
  or or_3 (CMD[5], and_24_out, and_23_out, and_22_out, and_21_out, and_20_out, and_19_out, and_18_out, and_17_out);
  and and_25 (and_25_out, decoder_1_out0, 1'b0);
  and and_26 (and_26_out, decoder_1_out1, 1'b1);
  and and_27 (and_27_out, decoder_1_out2, 1'b0);
  and and_28 (and_28_out, decoder_1_out3, 1'b1);
  and and_29 (and_29_out, decoder_1_out4, 1'b1);
  and and_30 (and_30_out, decoder_1_out5, 1'b0);
  and and_31 (and_31_out, decoder_1_out6, 1'b1);
  and and_32 (and_32_out, decoder_1_out7, 1'b1);
  or or_4 (CMD[4], and_32_out, and_31_out, and_30_out, and_29_out, and_28_out, and_27_out, and_26_out, and_25_out);
  and and_33 (and_33_out, decoder_1_out0, 1'b1);
  and and_34 (and_34_out, decoder_1_out1, 1'b0);
  and and_35 (and_35_out, decoder_1_out2, 1'b0);
  and and_36 (and_36_out, decoder_1_out3, 1'b0);
  and and_37 (and_37_out, decoder_1_out4, 1'b0);
  and and_38 (and_38_out, decoder_1_out5, 1'b1);
  and and_39 (and_39_out, decoder_1_out6, 1'b0);
  and and_40 (and_40_out, decoder_1_out7, 1'b1);
  or or_5 (CMD[3], and_40_out, and_39_out, and_38_out, and_37_out, and_36_out, and_35_out, and_34_out, and_33_out);
  and and_41 (and_41_out, decoder_1_out0, 1'b0);
  and and_42 (and_42_out, decoder_1_out1, 1'b0);
  and and_43 (and_43_out, decoder_1_out2, 1'b0);
  and and_44 (and_44_out, decoder_1_out3, 1'b0);
  and and_45 (and_45_out, decoder_1_out4, 1'b1);
  and and_46 (and_46_out, decoder_1_out5, 1'b0);
  and and_47 (and_47_out, decoder_1_out6, 1'b0);
  and and_48 (and_48_out, decoder_1_out7, 1'b1);
  or or_6 (CMD[2], and_48_out, and_47_out, and_46_out, and_45_out, and_44_out, and_43_out, and_42_out, and_41_out);
  and and_49 (and_49_out, decoder_1_out0, 1'b1);
  and and_50 (and_50_out, decoder_1_out1, 1'b0);
  and and_51 (and_51_out, decoder_1_out2, 1'b0);
  and and_52 (and_52_out, decoder_1_out3, 1'b0);
  and and_53 (and_53_out, decoder_1_out4, 1'b1);
  and and_54 (and_54_out, decoder_1_out5, 1'b0);
  and and_55 (and_55_out, decoder_1_out6, 1'b0);
  and and_56 (and_56_out, decoder_1_out7, 1'b1);
  or or_7 (CMD[1], and_56_out, and_55_out, and_54_out, and_53_out, and_52_out, and_51_out, and_50_out, and_49_out);
  and and_57 (and_57_out, decoder_1_out0, 1'b0);
  and and_58 (and_58_out, decoder_1_out1, 1'b0);
  and and_59 (and_59_out, decoder_1_out2, 1'b0);
  and and_60 (and_60_out, decoder_1_out3, 1'b1);
  and and_61 (and_61_out, decoder_1_out4, 1'b1);
  and and_62 (and_62_out, decoder_1_out5, 1'b1);
  and and_63 (and_63_out, decoder_1_out6, 1'b1);
  and and_64 (and_64_out, decoder_1_out7, 1'b1);
  or or_8 (CMD[0], and_64_out, and_63_out, and_62_out, and_61_out, and_60_out, and_59_out, and_58_out, and_57_out);
endmodule

module GPR (
  input  [7:0] D,
  input  [1:0] ADDR1,
  input  EN,
  input  CLK,
  output [7:0] Q
);

  wire and_1_out, and_2_out, and_3_out, and_4_out, and_5_out, and_6_out, and_7_out, and_8_out, and_9_out,
       and_10_out, and_11_out, and_12_out, and_13_out, and_14_out, and_15_out, and_16_out, and_17_out,
       and_18_out, and_19_out, and_20_out, and_21_out, and_22_out, and_23_out, and_24_out, and_25_out,
       and_26_out, and_27_out, and_28_out, and_29_out, and_30_out, and_31_out, and_32_out, and_33_out,
       and_34_out, and_35_out, and_36_out, decoder_1_out0, decoder_1_out1, decoder_1_out2, decoder_1_out3,
       dffwen_1_q, dffwen_2_q, dffwen_3_q, dffwen_4_q, dffwen_5_q, dffwen_6_q, dffwen_7_q, dffwen_8_q,
       dffwen_9_q, dffwen_10_q, dffwen_11_q, dffwen_12_q, dffwen_13_q, dffwen_14_q, dffwen_15_q, dffwen_16_q,
       dffwen_17_q, dffwen_18_q, dffwen_19_q, dffwen_20_q, dffwen_21_q, dffwen_22_q, dffwen_23_q,
       dffwen_24_q, dffwen_25_q, dffwen_26_q, dffwen_27_q, dffwen_28_q, dffwen_29_q, dffwen_30_q,
       dffwen_31_q, dffwen_32_q;

  Decoder #(.enable("false"), .select(2)) decoder_1 (
    .out0(decoder_1_out0), .out1(decoder_1_out1), .out2(decoder_1_out2), .out3(decoder_1_out3), .sel(ADDR1));
  and and_1 (and_1_out, decoder_1_out0, EN);
  and and_2 (and_2_out, decoder_1_out1, EN);
  and and_3 (and_3_out, decoder_1_out2, EN);
  and and_4 (and_4_out, decoder_1_out3, EN);
  DFFWEN dffwen_1 (.D(D[7]), .EN(and_1_out), .CLK(CLK), .Q(dffwen_1_q));
  DFFWEN dffwen_2 (.D(D[7]), .EN(and_2_out), .CLK(CLK), .Q(dffwen_2_q));
  DFFWEN dffwen_3 (.D(D[7]), .EN(and_3_out), .CLK(CLK), .Q(dffwen_3_q));
  DFFWEN dffwen_4 (.D(D[7]), .EN(and_4_out), .CLK(CLK), .Q(dffwen_4_q));
  and and_5 (and_5_out, decoder_1_out0, dffwen_1_q);
  and and_6 (and_6_out, decoder_1_out1, dffwen_2_q);
  and and_7 (and_7_out, decoder_1_out2, dffwen_3_q);
  and and_8 (and_8_out, decoder_1_out3, dffwen_4_q);
  or or_1 (Q[7], and_8_out, and_7_out, and_6_out, and_5_out);
  and and_9 (and_9_out, decoder_1_out0, dffwen_5_q);
  DFFWEN dffwen_5 (.D(D[6]), .EN(and_1_out), .CLK(CLK), .Q(dffwen_5_q));
  and and_10 (and_10_out, decoder_1_out1, dffwen_6_q);
  DFFWEN dffwen_6 (.D(D[6]), .EN(and_2_out), .CLK(CLK), .Q(dffwen_6_q));
  and and_11 (and_11_out, decoder_1_out2, dffwen_7_q);
  DFFWEN dffwen_7 (.D(D[6]), .EN(and_3_out), .CLK(CLK), .Q(dffwen_7_q));
  and and_12 (and_12_out, decoder_1_out3, dffwen_8_q);
  DFFWEN dffwen_8 (.D(D[6]), .EN(and_4_out), .CLK(CLK), .Q(dffwen_8_q));
  or or_2 (Q[6], and_12_out, and_11_out, and_10_out, and_9_out);
  DFFWEN dffwen_9 (.D(D[5]), .EN(and_1_out), .CLK(CLK), .Q(dffwen_9_q));
  DFFWEN dffwen_10 (.D(D[5]), .EN(and_2_out), .CLK(CLK), .Q(dffwen_10_q));
  DFFWEN dffwen_11 (.D(D[5]), .EN(and_3_out), .CLK(CLK), .Q(dffwen_11_q));
  DFFWEN dffwen_12 (.D(D[5]), .EN(and_4_out), .CLK(CLK), .Q(dffwen_12_q));
  and and_13 (and_13_out, decoder_1_out0, dffwen_9_q);
  and and_14 (and_14_out, decoder_1_out1, dffwen_10_q);
  and and_15 (and_15_out, decoder_1_out2, dffwen_11_q);
  and and_16 (and_16_out, decoder_1_out3, dffwen_12_q);
  or or_3 (Q[5], and_16_out, and_15_out, and_14_out, and_13_out);
  and and_17 (and_17_out, decoder_1_out0, dffwen_13_q);
  DFFWEN dffwen_13 (.D(D[4]), .EN(and_1_out), .CLK(CLK), .Q(dffwen_13_q));
  and and_18 (and_18_out, decoder_1_out1, dffwen_14_q);
  DFFWEN dffwen_14 (.D(D[4]), .EN(and_2_out), .CLK(CLK), .Q(dffwen_14_q));
  and and_19 (and_19_out, decoder_1_out2, dffwen_15_q);
  DFFWEN dffwen_15 (.D(D[4]), .EN(and_3_out), .CLK(CLK), .Q(dffwen_15_q));
  and and_20 (and_20_out, decoder_1_out3, dffwen_16_q);
  DFFWEN dffwen_16 (.D(D[4]), .EN(and_4_out), .CLK(CLK), .Q(dffwen_16_q));
  or or_4 (Q[4], and_17_out, and_20_out, and_18_out, and_19_out);
  and and_21 (and_21_out, decoder_1_out0, dffwen_17_q);
  DFFWEN dffwen_17 (.D(D[3]), .EN(and_1_out), .CLK(CLK), .Q(dffwen_17_q));
  and and_22 (and_22_out, decoder_1_out1, dffwen_18_q);
  DFFWEN dffwen_18 (.D(D[3]), .EN(and_2_out), .CLK(CLK), .Q(dffwen_18_q));
  and and_23 (and_23_out, decoder_1_out2, dffwen_19_q);
  DFFWEN dffwen_19 (.D(D[3]), .EN(and_3_out), .CLK(CLK), .Q(dffwen_19_q));
  and and_24 (and_24_out, decoder_1_out3, dffwen_20_q);
  DFFWEN dffwen_20 (.D(D[3]), .EN(and_4_out), .CLK(CLK), .Q(dffwen_20_q));
  or or_5 (Q[3], and_24_out, and_23_out, and_22_out, and_21_out);
  DFFWEN dffwen_21 (.D(D[2]), .EN(and_1_out), .CLK(CLK), .Q(dffwen_21_q));
  DFFWEN dffwen_22 (.D(D[2]), .EN(and_2_out), .CLK(CLK), .Q(dffwen_22_q));
  DFFWEN dffwen_23 (.D(D[2]), .EN(and_3_out), .CLK(CLK), .Q(dffwen_23_q));
  DFFWEN dffwen_24 (.D(D[2]), .EN(and_4_out), .CLK(CLK), .Q(dffwen_24_q));
  and and_25 (and_25_out, decoder_1_out0, dffwen_21_q);
  and and_26 (and_26_out, decoder_1_out1, dffwen_22_q);
  and and_27 (and_27_out, decoder_1_out2, dffwen_23_q);
  and and_28 (and_28_out, decoder_1_out3, dffwen_24_q);
  or or_6 (Q[2], and_28_out, and_27_out, and_26_out, and_25_out);
  DFFWEN dffwen_25 (.D(D[1]), .EN(and_1_out), .CLK(CLK), .Q(dffwen_25_q));
  DFFWEN dffwen_26 (.D(D[1]), .EN(and_2_out), .CLK(CLK), .Q(dffwen_26_q));
  DFFWEN dffwen_27 (.D(D[1]), .EN(and_3_out), .CLK(CLK), .Q(dffwen_27_q));
  DFFWEN dffwen_28 (.D(D[1]), .EN(and_4_out), .CLK(CLK), .Q(dffwen_28_q));
  and and_29 (and_29_out, decoder_1_out0, dffwen_25_q);
  and and_30 (and_30_out, decoder_1_out1, dffwen_26_q);
  and and_31 (and_31_out, decoder_1_out2, dffwen_27_q);
  and and_32 (and_32_out, decoder_1_out3, dffwen_28_q);
  or or_7 (Q[1], and_32_out, and_31_out, and_30_out, and_29_out);
  DFFWEN dffwen_29 (.D(D[0]), .EN(and_1_out), .CLK(CLK), .Q(dffwen_29_q));
  DFFWEN dffwen_30 (.D(D[0]), .EN(and_2_out), .CLK(CLK), .Q(dffwen_30_q));
  DFFWEN dffwen_31 (.D(D[0]), .EN(and_3_out), .CLK(CLK), .Q(dffwen_31_q));
  DFFWEN dffwen_32 (.D(D[0]), .EN(and_4_out), .CLK(CLK), .Q(dffwen_32_q));
  and and_33 (and_33_out, decoder_1_out0, dffwen_29_q);
  and and_34 (and_34_out, decoder_1_out1, dffwen_30_q);
  and and_35 (and_35_out, decoder_1_out2, dffwen_31_q);
  and and_36 (and_36_out, decoder_1_out3, dffwen_32_q);
  or or_8 (Q[0], and_36_out, and_35_out, and_34_out, and_33_out);
endmodule

module DFFWEN (
  input  D,
  input  EN,
  input  CLK,
  output Q
);

  wire multiplexer_1_out;

  D_Flip_Flop d_ff_1 (.D(multiplexer_1_out), .clk(CLK), .Q(Q));  // open: Qn, preset, reset
  Multiplexer multiplexer_1 (.in0(Q), .in1(D), .out(multiplexer_1_out), .sel(EN));
endmodule
